// Logisim project first half of the computer.circ as structural Verilog
module a_bit_of_memory (
  input  i,
  input  s,
  output o
);

  wire nand_1_out, nand_2_out, nand_4_out;

  nand nand_1 (nand_1_out, i, s);
  nand nand_2 (nand_2_out, nand_1_out, s);
  nand nand_3 (o, nand_1_out, nand_4_out);
  nand nand_4 (nand_4_out, o, nand_2_out);

  // Notes on the sheet:
  //   This is how a combination of four NAND gates (or NOT gates) can "remember";
  //   When s(set) is turned on we can write the data we want and remember it by turning s off.
  //   This is only one bit of memory,  but this is the basic building block of all computer memory.
endmodule

module a_byte_of_memory (
  input  i0,
  input  i1,
  input  i2,
  input  i3,
  input  i4,
  input  i5,
  input  i6,
  input  i7,
  input  s,
  output o0,
  output o1,
  output o2,
  output o3,
  output o4,
  output o5,
  output o6,
  output o7
);

  a_bit_of_memory a_bit_of_memory_1 (.i(i0), .s(s), .o(o0));
  a_bit_of_memory a_bit_of_memory_2 (.i(i1), .s(s), .o(o1));
  a_bit_of_memory a_bit_of_memory_3 (.i(i2), .s(s), .o(o2));
  a_bit_of_memory a_bit_of_memory_4 (.i(i3), .s(s), .o(o3));
  a_bit_of_memory a_bit_of_memory_5 (.i(i4), .s(s), .o(o4));
  a_bit_of_memory a_bit_of_memory_6 (.i(i5), .s(s), .o(o5));
  a_bit_of_memory a_bit_of_memory_7 (.i(i6), .s(s), .o(o6));
  a_bit_of_memory a_bit_of_memory_8 (.i(i7), .s(s), .o(o7));

  // Notes on the sheet:
  //   A bit of memory
  //   A bit of memory
  //   A bit of memory
  //   A bit of memory
  //   A bit of memory
  //   A bit of memory
  //   A bit of memory
  //   A bit of memory
  //   or have a nibble or take a whole byte.
  //   You've likely deduced what is this circuit about
  //   Just to show you that computer designers do have a sense of humor, 
  //   when they use 4 bits as a unit they call it nibble.So you can eat a tiny bit of cherry pie,
  //   The byte, taken as a whole, is a location in space that can be in any one of the 2^8 = 256 states at any given time.
endmodule

module Register (
  input  i0,
  input  i1,
  input  i2,
  input  i3,
  input  i4,
  input  i5,
  input  i6,
  input  i7,
  input  e,
  input  s,
  output o0,
  output o1,
  output o2,
  output o3,
  output o4,
  output o5,
  output o6,
  output o7
);

  wire and_1_out, and_2_out, and_3_out, and_4_out, and_5_out, and_6_out, and_7_out, and_8_out;

  and and_1 (and_1_out, i0, e);
  and and_2 (and_2_out, i1, e);
  and and_3 (and_3_out, i2, e);
  and and_4 (and_4_out, i3, e);
  and and_5 (and_5_out, i4, e);
  and and_6 (and_6_out, i5, e);
  and and_7 (and_7_out, i6, e);
  and and_8 (and_8_out, i7, e);
  a_byte_of_memory a_byte_of_memory_1 (
    .i0(and_1_out), .i1(and_2_out), .i2(and_3_out), .i3(and_4_out), .i4(and_5_out), .i5(and_6_out),
    .i6(and_7_out), .i7(and_8_out), .s(s), .o0(o0), .o1(o1), .o2(o2), .o3(o3), .o4(o4), .o5(o5), .o6(o6),
    .o7(o7));

  // Notes on the sheet:
  //   Enabler
  //   |
  //   |
  //   |
  //   |
  //   |
  //   |
  //   |
  //   |
  //   |
  //   |
  //   |
  //   |
  //   A byte of memory
  //   Every time you store a new set of values the old one is replaced.
  //    an enabler allows a byte through when the bit 'e' is 1 and stops the byte when it is 0.
  //   Register simply means a place to record some kind of information.However it's very limited,
  //   A "Register" differs from "a byte of memory" by  the eight AND gates on the left hand side,acting as an enabler;
endmodule

module a_bus (
  input  in_1,
  input  in_2,
  input  in_3,
  input  in_4,
  input  in_5,
  input  in_6,
  input  in_7,
  input  in_8,
  input  in_9,
  input  in_10,
  input  in_11,
  input  in_12,
  input  in_13,
  input  in_14,
  input  in_15,
  input  in_16,
  input  in_17,
  input  in_18,
  input  in_19,
  input  in_20,
  input  in_21,
  input  in_22,
  input  in_23,
  input  in_24,
  input  in_25,
  input  in_26,
  input  in_27,
  input  in_28,
  input  in_29,
  input  in_30,
  input  in_31,
  input  in_32,
  input  in_33,
  input  in_34,
  input  in_35,
  input  in_36,
  input  in_37,
  input  in_38,
  input  in_39,
  input  in_40,
  input  memory_or_register,
  input  enabler,
  input  [3:0] in_43,
  input  in_44,
  input  with_a_splitter,
  input  in_46,
  input  in_47,
  input  [3:0] data_we_want_write_for_ex,
  input  [3:0] data_we_want_to_read_for_ex,
  input  in_50,
  input  gate_buffer,
  input  gate_buffer_2,
  input  gate_buffer_3,
  input  gate_buffer_4,
  input  e,
  input  s,
  input  in_57,
  input  in_58,
  input  in_59,
  input  in_60,
  input  in_61,
  input  in_62,
  input  setter,
  input  _128,
  input  _64,
  input  _32,
  input  setter_2,
  input  in_68,
  input  _16,
  input  in_70,
  input  _8,
  input  _4,
  input  in_73,
  input  in_74,
  input  in_75,
  input  _2,
  input  in_77,
  input  in_78,
  input  in_79,
  input  _1,
  input  in_81,
  input  in_82,
  input  in_83,
  input  in_84,
  input  in_85,
  input  in_86,
  input  in_87,
  input  in_88,
  input  in_89,
  input  in_90,
  input  in_91,
  input  in_92,
  input  in_93,
  input  in_94,
  input  in_95,
  input  in_96,
  input  in_97,
  input  in_98,
  output out_99,
  output out_100,
  output out_101,
  output out_102,
  output out_103,
  output out_104,
  output out_105,
  output out_106,
  output out_107,
  output out_108,
  output out_109,
  output out_110,
  output out_111,
  output out_112,
  output out_113,
  output out_114,
  output bus_for_ex,
  output [3:0] displayed_data__data_that_goes_to_bus_for_ex,
  output out_117,
  output out_118,
  output out_119,
  output out_120,
  output out_121,
  output out_122,
  output out_123,
  output out_124
);

  wire multiplexer_2_out, multiplexer_3_out, multiplexer_4_out, multiplexer_5_out, multiplexer_6_out,
       multiplexer_7_out, multiplexer_8_out, multiplexer_9_out, multiplexer_10_out, multiplexer_11_out,
       multiplexer_12_out, multiplexer_13_out, multiplexer_14_out, multiplexer_15_out, multiplexer_16_out,
       multiplexer_17_out, multiplexer_18_out, multiplexer_19_out, multiplexer_20_out, multiplexer_21_out,
       multiplexer_22_out, multiplexer_23_out, multiplexer_24_out, multiplexer_25_out, multiplexer_26_out,
       multiplexer_27_out, multiplexer_28_out, multiplexer_29_out, multiplexer_30_out, multiplexer_31_out,
       multiplexer_32_out, multiplexer_33_out, not_1_out, not_2_out, not_3_out, not_4_out, register_5_o0,
       register_5_o1, register_5_o2, register_5_o3, register_5_o4, register_5_o5, register_5_o6,
       register_5_o7, register_6_o0, register_6_o1, register_6_o2, register_6_o3, register_6_o4,
       register_6_o5, register_6_o6, register_6_o7, register_7_o0, register_7_o1, register_7_o2,
       register_7_o3, register_7_o4, register_7_o5, register_7_o6, register_7_o7, register_8_o0,
       register_8_o1, register_8_o2, register_8_o3, register_8_o4, register_8_o5, register_8_o6,
       register_8_o7;
  wire [7:0] controlled_buffer_2_out, controlled_buffer_3_out, controlled_buffer_12_out,
       controlled_buffer_13_out, controlled_buffer_22_out, controlled_buffer_23_out,
       controlled_buffer_32_out, controlled_buffer_33_out;

  not not_1 (not_1_out, setter);
  Register register_1 (
    .i0(in_9), .i1(in_13), .i2(in_17), .i3(in_21), .i4(in_25), .i5(in_29), .i6(in_33), .i7(in_37), .e(in_1),
    .s(in_2), .o0(in_9), .o1(in_33), .o2(in_29), .o3(in_25), .o4(in_21), .o5(in_17), .o6(in_13), .o7(in_37));
  assign bus_for_ex = enabler ? memory_or_register : 1'bz;  // Controlled_Buffer controlled_buffer_1
  assign controlled_buffer_2_out = not_1_out ? {out_124, out_123, out_122, out_121, out_120, out_119, out_118, out_117} : 8'bz;  // Controlled_Buffer controlled_buffer_2
  Hex_Digit_Display hex_digit_display_1 (.value(in_43));  // open: dp
  Multiplexer #(.width(4)) multiplexer_1 (
    .in0(data_we_want_write_for_ex), .in1(data_we_want_to_read_for_ex),
    .out(displayed_data__data_that_goes_to_bus_for_ex), .sel(in_50));  // open: en
  Register register_2 (
    .i0(in_9), .i1(in_13), .i2(in_17), .i3(in_21), .i4(in_25), .i5(in_29), .i6(in_33), .i7(in_37), .e(in_3),
    .s(in_4), .o0(in_9), .o1(in_33), .o2(in_29), .o3(in_25), .o4(in_21), .o5(in_17), .o6(in_13), .o7(in_37));
  Hex_Digit_Display hex_digit_display_2 (.value({in_47, in_46, with_a_splitter, in_44}));  // open: dp
  Multiplexer multiplexer_2 (
    .in0(controlled_buffer_2_out[0]), .in1(controlled_buffer_3_out[0]), .out(multiplexer_2_out), .sel(setter));  // open: en
  Multiplexer multiplexer_3 (
    .in0(controlled_buffer_2_out[1]), .in1(controlled_buffer_3_out[1]), .out(multiplexer_3_out), .sel(setter));  // open: en
  Multiplexer multiplexer_4 (
    .in0(controlled_buffer_2_out[2]), .in1(controlled_buffer_3_out[2]), .out(multiplexer_4_out), .sel(setter));  // open: en
  Multiplexer multiplexer_5 (
    .in0(controlled_buffer_2_out[3]), .in1(controlled_buffer_3_out[3]), .out(multiplexer_5_out), .sel(setter));  // open: en
  Multiplexer multiplexer_6 (
    .in0(controlled_buffer_2_out[4]), .in1(controlled_buffer_3_out[4]), .out(multiplexer_6_out), .sel(setter));  // open: en
  Multiplexer multiplexer_7 (
    .in0(controlled_buffer_2_out[5]), .in1(controlled_buffer_3_out[5]), .out(multiplexer_7_out), .sel(setter));  // open: en
  Multiplexer multiplexer_8 (
    .in0(controlled_buffer_2_out[6]), .in1(controlled_buffer_3_out[6]), .out(multiplexer_8_out), .sel(setter));  // open: en
  Multiplexer multiplexer_9 (
    .in0(controlled_buffer_2_out[7]), .in1(controlled_buffer_3_out[7]), .out(multiplexer_9_out), .sel(setter));  // open: en
  assign controlled_buffer_3_out = setter ? {_1, _2, _4, _8, _16, _32, _64, _128} : 8'bz;  // Controlled_Buffer controlled_buffer_3
  Register register_3 (
    .i0(in_9), .i1(in_13), .i2(in_17), .i3(in_21), .i4(in_25), .i5(in_29), .i6(in_33), .i7(in_37), .e(in_5),
    .s(in_6), .o0(in_9), .o1(in_33), .o2(in_29), .o3(in_25), .o4(in_21), .o5(in_17), .o6(in_13), .o7(in_37));
  Register register_4 (
    .i0(in_9), .i1(in_13), .i2(in_17), .i3(in_21), .i4(in_25), .i5(in_29), .i6(in_33), .i7(in_37), .e(in_7),
    .s(in_8), .o0(in_9), .o1(in_33), .o2(in_29), .o3(in_25), .o4(in_21), .o5(in_17), .o6(in_13), .o7(in_37));
  Register register_5 (
    .i0(multiplexer_2_out), .i1(multiplexer_3_out), .i2(multiplexer_4_out), .i3(multiplexer_5_out),
    .i4(multiplexer_6_out), .i5(multiplexer_7_out), .i6(multiplexer_8_out), .i7(multiplexer_9_out), .e(e),
    .s(s), .o0(register_5_o0), .o1(register_5_o1), .o2(register_5_o2), .o3(register_5_o3),
    .o4(register_5_o4), .o5(register_5_o5), .o6(register_5_o6), .o7(register_5_o7));
  assign out_117 = gate_buffer ? register_5_o0 : 1'bz;  // Controlled_Buffer controlled_buffer_4
  assign out_118 = gate_buffer ? register_5_o1 : 1'bz;  // Controlled_Buffer controlled_buffer_5
  assign out_119 = gate_buffer ? register_5_o2 : 1'bz;  // Controlled_Buffer controlled_buffer_6
  assign out_120 = gate_buffer ? register_5_o3 : 1'bz;  // Controlled_Buffer controlled_buffer_7
  assign out_121 = gate_buffer ? register_5_o4 : 1'bz;  // Controlled_Buffer controlled_buffer_8
  assign out_122 = gate_buffer ? register_5_o5 : 1'bz;  // Controlled_Buffer controlled_buffer_9
  assign out_123 = gate_buffer ? register_5_o6 : 1'bz;  // Controlled_Buffer controlled_buffer_10
  assign out_124 = gate_buffer ? register_5_o7 : 1'bz;  // Controlled_Buffer controlled_buffer_11
  assign controlled_buffer_12_out = not_2_out ? {out_124, out_123, out_122, out_121, out_120, out_119, out_118, out_117} : 8'bz;  // Controlled_Buffer controlled_buffer_12
  not not_2 (not_2_out, setter_2);
  Multiplexer multiplexer_10 (
    .in0(controlled_buffer_12_out[0]), .in1(controlled_buffer_13_out[0]), .out(multiplexer_10_out),
    .sel(setter_2));  // open: en
  Multiplexer multiplexer_11 (
    .in0(controlled_buffer_12_out[1]), .in1(controlled_buffer_13_out[1]), .out(multiplexer_11_out),
    .sel(setter_2));  // open: en
  Multiplexer multiplexer_12 (
    .in0(controlled_buffer_12_out[2]), .in1(controlled_buffer_13_out[2]), .out(multiplexer_12_out),
    .sel(setter_2));  // open: en
  Multiplexer multiplexer_13 (
    .in0(controlled_buffer_12_out[3]), .in1(controlled_buffer_12_out[4]), .out(multiplexer_13_out),
    .sel(setter_2));  // open: en
  Multiplexer multiplexer_14 (
    .in0(controlled_buffer_12_out[4]), .in1(controlled_buffer_13_out[4]), .out(multiplexer_14_out),
    .sel(setter_2));  // open: en
  Multiplexer multiplexer_15 (
    .in0(controlled_buffer_12_out[5]), .in1(controlled_buffer_13_out[5]), .out(multiplexer_15_out),
    .sel(setter_2));  // open: en
  Multiplexer multiplexer_16 (
    .in0(controlled_buffer_12_out[6]), .in1(controlled_buffer_13_out[6]), .out(multiplexer_16_out),
    .sel(setter_2));  // open: en
  Multiplexer multiplexer_17 (
    .in0(controlled_buffer_12_out[7]), .in1(controlled_buffer_13_out[7]), .out(multiplexer_17_out),
    .sel(setter_2));  // open: en
  assign {controlled_buffer_13_out[7:4], controlled_buffer_12_out[4], controlled_buffer_13_out[2:0]} = setter_2 ? {in_96, in_93, in_90, in_87, in_84, in_81, in_77, in_73} : 8'bz;  // Controlled_Buffer controlled_buffer_13
  Register register_6 (
    .i0(multiplexer_10_out), .i1(multiplexer_11_out), .i2(multiplexer_12_out), .i3(multiplexer_13_out),
    .i4(multiplexer_14_out), .i5(multiplexer_15_out), .i6(multiplexer_16_out), .i7(multiplexer_17_out),
    .e(in_57), .s(in_58), .o0(register_6_o0), .o1(register_6_o1), .o2(register_6_o2), .o3(register_6_o3),
    .o4(register_6_o4), .o5(register_6_o5), .o6(register_6_o6), .o7(register_6_o7));
  assign out_117 = gate_buffer_2 ? register_6_o0 : 1'bz;  // Controlled_Buffer controlled_buffer_14
  assign out_118 = gate_buffer_2 ? register_6_o1 : 1'bz;  // Controlled_Buffer controlled_buffer_15
  assign out_119 = gate_buffer_2 ? register_6_o2 : 1'bz;  // Controlled_Buffer controlled_buffer_16
  assign out_120 = gate_buffer_2 ? register_6_o3 : 1'bz;  // Controlled_Buffer controlled_buffer_17
  assign out_121 = gate_buffer_2 ? register_6_o4 : 1'bz;  // Controlled_Buffer controlled_buffer_18
  assign out_122 = gate_buffer_2 ? register_6_o5 : 1'bz;  // Controlled_Buffer controlled_buffer_19
  assign out_123 = gate_buffer_2 ? register_6_o6 : 1'bz;  // Controlled_Buffer controlled_buffer_20
  assign out_124 = gate_buffer_2 ? register_6_o7 : 1'bz;  // Controlled_Buffer controlled_buffer_21
  assign controlled_buffer_22_out = not_3_out ? {out_124, out_123, out_122, out_121, out_120, out_119, out_118, out_117} : 8'bz;  // Controlled_Buffer controlled_buffer_22
  not not_3 (not_3_out, in_70);
  Multiplexer multiplexer_18 (
    .in0(controlled_buffer_22_out[0]), .in1(controlled_buffer_23_out[0]), .out(multiplexer_18_out),
    .sel(in_70));  // open: en
  Multiplexer multiplexer_19 (
    .in0(controlled_buffer_22_out[1]), .in1(controlled_buffer_23_out[1]), .out(multiplexer_19_out),
    .sel(in_70));  // open: en
  Multiplexer multiplexer_20 (
    .in0(controlled_buffer_22_out[2]), .in1(controlled_buffer_23_out[2]), .out(multiplexer_20_out),
    .sel(in_70));  // open: en
  Multiplexer multiplexer_21 (
    .in0(controlled_buffer_22_out[3]), .in1(controlled_buffer_23_out[3]), .out(multiplexer_21_out),
    .sel(in_70));  // open: en
  Multiplexer multiplexer_22 (
    .in0(controlled_buffer_22_out[4]), .in1(controlled_buffer_23_out[4]), .out(multiplexer_22_out),
    .sel(in_70));  // open: en
  Multiplexer multiplexer_23 (
    .in0(controlled_buffer_22_out[5]), .in1(controlled_buffer_23_out[5]), .out(multiplexer_23_out),
    .sel(in_70));  // open: en
  Multiplexer multiplexer_24 (
    .in0(controlled_buffer_22_out[6]), .in1(controlled_buffer_23_out[6]), .out(multiplexer_24_out),
    .sel(in_70));  // open: en
  Multiplexer multiplexer_25 (
    .in0(controlled_buffer_22_out[7]), .in1(controlled_buffer_23_out[7]), .out(multiplexer_25_out),
    .sel(in_70));  // open: en
  assign controlled_buffer_23_out = in_70 ? {in_98, in_95, in_92, in_89, in_86, in_83, in_79, in_75} : 8'bz;  // Controlled_Buffer controlled_buffer_23
  Register register_7 (
    .i0(multiplexer_18_out), .i1(multiplexer_19_out), .i2(multiplexer_20_out), .i3(multiplexer_21_out),
    .i4(multiplexer_22_out), .i5(multiplexer_23_out), .i6(multiplexer_24_out), .i7(multiplexer_25_out),
    .e(in_61), .s(in_62), .o0(register_7_o0), .o1(register_7_o1), .o2(register_7_o2), .o3(register_7_o3),
    .o4(register_7_o4), .o5(register_7_o5), .o6(register_7_o6), .o7(register_7_o7));
  assign out_117 = gate_buffer_4 ? register_7_o0 : 1'bz;  // Controlled_Buffer controlled_buffer_24
  assign out_118 = gate_buffer_4 ? register_7_o1 : 1'bz;  // Controlled_Buffer controlled_buffer_25
  assign out_119 = gate_buffer_4 ? register_7_o2 : 1'bz;  // Controlled_Buffer controlled_buffer_26
  assign out_120 = gate_buffer_4 ? register_7_o3 : 1'bz;  // Controlled_Buffer controlled_buffer_27
  assign out_121 = gate_buffer_4 ? register_7_o4 : 1'bz;  // Controlled_Buffer controlled_buffer_28
  assign out_122 = gate_buffer_4 ? register_7_o5 : 1'bz;  // Controlled_Buffer controlled_buffer_29
  assign out_123 = gate_buffer_4 ? register_7_o6 : 1'bz;  // Controlled_Buffer controlled_buffer_30
  assign out_124 = gate_buffer_4 ? register_7_o7 : 1'bz;  // Controlled_Buffer controlled_buffer_31
  not not_4 (not_4_out, in_68);
  assign controlled_buffer_32_out = not_4_out ? {out_124, out_123, out_122, out_121, out_120, out_119, out_118, out_117} : 8'bz;  // Controlled_Buffer controlled_buffer_32
  Multiplexer multiplexer_26 (
    .in0(controlled_buffer_32_out[0]), .in1(controlled_buffer_33_out[0]), .out(multiplexer_26_out),
    .sel(in_68));  // open: en
  Multiplexer multiplexer_27 (
    .in0(controlled_buffer_32_out[1]), .in1(controlled_buffer_33_out[1]), .out(multiplexer_27_out),
    .sel(in_68));  // open: en
  Multiplexer multiplexer_28 (
    .in0(controlled_buffer_32_out[2]), .in1(controlled_buffer_33_out[2]), .out(multiplexer_28_out),
    .sel(in_68));  // open: en
  Multiplexer multiplexer_29 (
    .in0(controlled_buffer_32_out[3]), .in1(controlled_buffer_33_out[3]), .out(multiplexer_29_out),
    .sel(in_68));  // open: en
  Multiplexer multiplexer_30 (
    .in0(controlled_buffer_32_out[4]), .in1(controlled_buffer_33_out[4]), .out(multiplexer_30_out),
    .sel(in_68));  // open: en
  Multiplexer multiplexer_31 (
    .in0(controlled_buffer_32_out[5]), .in1(controlled_buffer_33_out[5]), .out(multiplexer_31_out),
    .sel(in_68));  // open: en
  Multiplexer multiplexer_32 (
    .in0(controlled_buffer_32_out[6]), .in1(controlled_buffer_33_out[6]), .out(multiplexer_32_out),
    .sel(in_68));  // open: en
  Multiplexer multiplexer_33 (
    .in0(controlled_buffer_32_out[7]), .in1(controlled_buffer_33_out[7]), .out(multiplexer_33_out),
    .sel(in_68));  // open: en
  assign controlled_buffer_33_out = in_68 ? {in_97, in_94, in_91, in_88, in_85, in_82, in_78, in_74} : 8'bz;  // Controlled_Buffer controlled_buffer_33
  Register register_8 (
    .i0(multiplexer_26_out), .i1(multiplexer_27_out), .i2(multiplexer_28_out), .i3(multiplexer_29_out),
    .i4(multiplexer_30_out), .i5(multiplexer_31_out), .i6(multiplexer_32_out), .i7(multiplexer_33_out),
    .e(in_59), .s(in_60), .o0(register_8_o0), .o1(register_8_o1), .o2(register_8_o2), .o3(register_8_o3),
    .o4(register_8_o4), .o5(register_8_o5), .o6(register_8_o6), .o7(register_8_o7));
  assign out_117 = gate_buffer_3 ? register_8_o0 : 1'bz;  // Controlled_Buffer controlled_buffer_34
  assign out_118 = gate_buffer_3 ? register_8_o1 : 1'bz;  // Controlled_Buffer controlled_buffer_35
  assign out_119 = gate_buffer_3 ? register_8_o2 : 1'bz;  // Controlled_Buffer controlled_buffer_36
  assign out_120 = gate_buffer_3 ? register_8_o3 : 1'bz;  // Controlled_Buffer controlled_buffer_37
  assign out_121 = gate_buffer_3 ? register_8_o4 : 1'bz;  // Controlled_Buffer controlled_buffer_38
  assign out_122 = gate_buffer_3 ? register_8_o5 : 1'bz;  // Controlled_Buffer controlled_buffer_39
  assign out_123 = gate_buffer_3 ? register_8_o6 : 1'bz;  // Controlled_Buffer controlled_buffer_40
  assign out_124 = gate_buffer_3 ? register_8_o7 : 1'bz;  // Controlled_Buffer controlled_buffer_41

  assign in_10 = in_9;
  assign in_11 = in_9;
  assign in_12 = in_9;
  assign in_14 = in_13;
  assign in_15 = in_13;
  assign in_16 = in_13;
  assign in_18 = in_17;
  assign in_19 = in_17;
  assign in_20 = in_17;
  assign in_22 = in_21;
  assign in_23 = in_21;
  assign in_24 = in_21;
  assign in_26 = in_25;
  assign in_27 = in_25;
  assign in_28 = in_25;
  assign in_30 = in_29;
  assign in_31 = in_29;
  assign in_32 = in_29;
  assign in_34 = in_33;
  assign in_35 = in_33;
  assign in_36 = in_33;
  assign in_38 = in_37;
  assign in_39 = in_37;
  assign in_40 = in_37;
  assign out_99 = in_9;
  assign out_100 = in_9;
  assign out_101 = in_13;
  assign out_102 = in_13;
  assign out_103 = in_17;
  assign out_104 = in_17;
  assign out_105 = in_21;
  assign out_106 = in_21;
  assign out_107 = in_25;
  assign out_108 = in_25;
  assign out_109 = in_29;
  assign out_110 = in_29;
  assign out_111 = in_33;
  assign out_112 = in_33;
  assign out_113 = in_37;
  assign out_114 = in_37;

  // Notes on the sheet:
  //   without a splitter
  //   These components will be briefly explained before their use.
  //   However, only one byte (8 bits of data) can be transmitted on the bus at a time.
  //   Splitter
  //   the splitter comes to play
  //   Write and Read wires with a multiplexer
  //   A bus is a vehicule that commonly travels along a predetermined route, and makes many stops where people get on or off. 
  //   Using the same logic, a bus topology facilitates data transfer between registers, such as sending data from R1 to R4, R3, and R2.
  //   Controlled buffer and why we can't use the top bus topology
  //   To optimize this setup, we introduce two essential components: a controlled buffer, which allows data transmission only when enabled, 
  //    and a splitter, which combines multiple wires into a single bus or splits a bus into individual wires, enabling connections to registers. 
  //   When it’s off, it blocks the way—perfect for avoiding traffic jams!
  //   We have a hexadecimal display that shows numbers from 0 to F, where A to F correspond to 10 to 15 in decimal. 
  //   This display has 4 input bits. If we have 4 different 4-bit inputs that we want to display on the same hex display, 
  //   in Logisim, if we didn’t use controlled buffers, the outputs of registers would cause trouble. When a register’s output isn’t powered,
  //   it sends a 0 in Logisim, which can crash into other data on the bus (called a collision). In real life, unpowered outputs are just “off,”
  //   When it’s 1, it lets you read data from the bus (taking data out to use). Think of it as a switch that decides if the register is grabbing data or sending it!
  //   golden rule :
  //   only one gate buffer can be active at time or chaos will happen
  //   Step 2: Share the Data on the Bus
  //   Step 3: Move the Data to Register B
  //   Step 4: Avoid a Collision!
  //   Step 5: New Data Comes Along
  //   but in Logisim, we need controlled buffers because when they’re turned off, they send null (no signal at all, not a 0), keeping the bus safe and quiet.
  //   When the setter is 0, the register can read from the bus.
  //   Inputs for writing on the Register A
  //   Step 1: Write a Number into Register A
  //   These are like gates on the highway. When you turn on the “enabler” (a signal that says “go!”), the buffer lets data flow from a register or memory onto the bus.
  //   A multiplexer is like a smart traffic director that switches things based on a signal. When the signal is 0, it lets you write data into a register (putting data from the bus into storage).
  //   When the setter is 1, the 8 to the bottom inputs can write data on the register. 
  //   "The setter " is a signal that controls the multiplexer and helps the register decide if it’s reading from the bus.
  //   make sure Register B’s setter is 0, enable the set and enable bits, then turn them off. Now Register B has the 10, replacing the old 5.
  //   The golden rule is: only one gate buffer can be turned on at a time, or things get messy. So, you turn off Register B’s buffer to keep the bus clear.
  //   turn on the set and enable bits built into Register A, and then turn them off. Now 5 is safely stored in Register A—yay, you’ve done an "es not es" to save the data!
  //   If you want to let this 5 go to the bus, you enable the gate buffer for Register A by turning on it on. This is like saying "hodor hold the door"—you’re opening the gate,
  //   Later, new data, like 10 (00001010 in binary), comes onto the bus (maybe from another register or memory). To save this into Register B, you repeat the "es not es" process:
  //   If you want to share this 10 on the bus, you do a "hodor hold the door" by enabling Register B’s gate buffer—but make sure all other buffers are off to avoid chaos!
  //   Let's first look into the refined bus topology and then explain it later
  //   Now you want to move that 5 to another register, let’s say Register B. The 5 is already on the bus, so you make sure the setter for Register B is 0 (this tells the MUX to let Register B read from the bus).
  //   To save the 5 into Register B, you do the same "es not es" method: enable the set and enable bits for Register B, then turn them off. The 5 is now safely stored in Register B—great job!
  //   You start by writing a number, like 5 (which is 4+1, or 00000101 in binary), into a register—let’s call it Register A. To save this number in Register A, you enable the setter (which automatically enables the MUX to let data in),
  //   and now the 5 is available on the Magic Bus for everyone to see! Since Register A’s output is connected through a controlled buffer(gate buffer), there’s no collision as long as no other buffers(gate buffers) are on.
  //   Since Register B now has data (the 5), you need to make sure its gate buffer is turned off. If Register B’s buffer were on at the same time as another buffer (like Register A’s), we’d have a collision—chaos on the bus!
  //   It’s like a well-organized train station where trains (data) move one at a time. You say "es not es" to save a number into a station (register),
  //   and "hodor hold the door" to let it travel on the tracks (bus)—but only one train can move at a time, thanks to those gate buffers!
  //   How it all works together
  //   Inputs for writing on the Register B
endmodule

module decoder (
  input  A1,
  input  A0,
  output D0,
  output D1,
  output D2,
  output D3
);

  wire not_1_out, not_2_out;

  not not_1 (not_1_out, A1);
  not not_2 (not_2_out, A0);
  and and_1 (D0, not_1_out, not_2_out);
  and and_2 (D1, A1, not_2_out);
  and and_3 (D2, A0, not_1_out);
  and and_4 (D3, A0, A1);

  // Notes on the sheet:
  //   . There are 4 output lines, labeled D0, D1, D2, and D3.
  //   What’s a Decoder, Anyway?
  //   Let’s Build a 2x4 Decoder!
  //   How It Works
  //   . The decoder looks at the input and turns on exactly one output:
  //   . If A1A0 = 00 (0), D0 turns on (1), and D1, D2, D3 are off (0).
  //   . If A1A0 = 01 (1), D1 turns on, and D0, D2, D3 are off.
  //   . If A1A0 = 10 (2), D2 turns on, and D0, D1, D3 are off.
  //   . If A1A0 = 11 (3), D3 turns on, and D0, D1, D2 are off.
  //   . You have 2 input bits, let’s call them A1 and A0. Together, they make a number from 0 to 3 (in binary: 00, 01, 10, 11).
  //   A 2x4 decoder takes 2 bits as input and picks one out of 4 outputs to turn on (make it 1). The other outputs stay off (0). It’s like having 4 toys, and your 2-bit code decides which one gets a spotlight!
  //   For example, if you have a 2-bit code, a decoder can pick one out of 4 toys. If you have a 3-bit code, it can pick one out of 8 toys. It’s super helpful in computers for things like choosing which register or memory spot to use!
  //   Imagine you’re playing a game where you have a secret code, and you need to pick one toy out of a bunch to light up. A decoder is like a magic toy picker—it takes a small code (a few bits) and uses it to pick one specific toy (or output) to turn on.
endmodule

module _3x8_decoder (
  input  Enabler,
  input  A2,
  input  A1,
  input  A0,
  output D0,
  output D1,
  output D2,
  output D3,
  output D4,
  output D5,
  output D6,
  output D7
);

  wire not_1_out, not_2_out, not_3_out;

  not not_1 (not_1_out, A2);
  not not_2 (not_2_out, A1);
  not not_3 (not_3_out, A0);
  and and_1 (D0, not_1_out, not_2_out, not_3_out, Enabler);
  and and_2 (D1, not_1_out, not_2_out, A0, Enabler);
  and and_3 (D2, not_1_out, A1, not_3_out, Enabler);
  and and_4 (D3, not_1_out, A1, A0, Enabler);
  and and_5 (D4, A2, not_2_out, not_3_out, Enabler);
  and and_6 (D5, A2, not_2_out, A0, Enabler);
  and and_7 (D6, A2, A1, not_3_out, Enabler);
  and and_8 (D7, A2, A1, A0, Enabler);

  // Notes on the sheet:
  //   . There are 8 output lines: D0, D1, D2, D3, D4, D5, D6, and D7.
  //   . If A2A1A0 = 000 (0), D0 turns on, and the rest are off.
  //   . If A2A1A0 = 001 (1), D1 turns on, and the rest are off.
  //   Now Let’s Build a 3x8 Decoder!
  //   How It Works
  //   . And so on, up to A2A1A0 = 111 (7), where D7 turns on.
  //   . But if the enabler is 0 (off), the decoder doesn’t work, and all outputs stay off (0)—no toys get picked!
  //   . You have 3 input bits: A2, A1, and A0. Together, they make a number from 0 to 7 (in binary: 000, 001, 010, 011, 100, 101, 110, 111).
  //   . You also have an enabler (a special switch). When the enabler is 1 (on), the decoder works normally and picks one output to turn on:
  //   A 3x8 decoder takes 3 bits as input and picks one out of 8 outputs to turn on—but only if the enabler says it’s okay! It’s like having 8 toys, and your 3-bit code decides which one gets the spotlight, but only when the toy picker is powered on.
endmodule

module _4x16_decoder (
  input  in_1,
  input  in_2,
  input  in_3,
  input  E,
  output D0,
  output D1,
  output D2,
  output D3,
  output D4,
  output D5,
  output D6,
  output D7,
  output D8,
  output D9,
  output D10,
  output D11,
  output D12,
  output D13,
  output D14,
  output D15
);

  wire not_1_out;

  not not_1 (not_1_out, E);
  _3x8_decoder u_3x8_decoder_1 (
    .Enabler(not_1_out), .A2(in_3), .A1(in_2), .A0(in_1), .D0(D0), .D1(D1), .D2(D2), .D3(D3), .D4(D4),
    .D5(D5), .D6(D6), .D7(D7));
  _3x8_decoder u_3x8_decoder_2 (
    .Enabler(E), .A2(in_3), .A1(in_2), .A0(in_1), .D0(D8), .D1(D9), .D2(D10), .D3(D11), .D4(D12), .D5(D13),
    .D6(D14), .D7(D15));

  // Notes on the sheet:
  //   . There are 16 output lines: D0 to D15.
  //   . Decoder 1 handles D0 to D7 (when E is 0).
  //   . Decoder 2 handles D8 to D15 (when E is 1).
  //   Now Let’s Build a 3x8 Decoder!
  //   How It Works
  //   . We’re using A3 as the enabler E, which decides which 3x8 decoder gets to work:
  //   . When E (A3) is 1, Decoder 2 is on, and Decoder 1 is off.
  //   . A2, A1, and A0 are the 3 bits that go into both decoders to pick one of their 8 outputs.
  //   . You have 4 input bits: A3, A2, A1, and A0. Together, they make a number from 0 to 15 (0000 to 1111 in binary).
  //   . When E (A3) is 0, the first decoder (Decoder 1) is on, and the second (Decoder 2) is off.
  //   Now let’s build a 4x16 decoder that takes 4 bits as input and picks one out of 16 outputs to turn on—again, only if the enabler says it’s okay! It’s like having 16 toys, and your 4-bit code picks the lucky one, but only when the toy picker is powered on. We’ll use two 3x8 decoders and a little trick to make this work.
endmodule

module _64_bit_RAM (
  input  in_1,
  input  in_2,
  input  in_3,
  input  in_4,
  input  in_5,
  input  MUX___track_switch,
  input  MUX___track_switch_2,
  input  MUX___track_switch_3,
  input  MUX___track_switch_4,
  input  [3:0] in_10,
  input  [3:0] in_11,
  input  [3:0] in_12,
  input  [3:0] in_13,
  input  MUX___track_switch_5,
  input  MUX___track_switch_6,
  input  MUX___track_switch_7,
  input  MUX___track_switch_8,
  input  [3:0] in_18,
  input  [3:0] in_19,
  input  [3:0] in_20,
  input  [3:0] in_21,
  input  MUX___track_switch_9,
  input  MUX___track_switch_10,
  input  MUX___track_switch_11,
  input  MUX___track_switch_12,
  input  [3:0] in_26,
  input  [3:0] in_27,
  input  [3:0] in_28,
  input  [3:0] in_29,
  input  MUX___track_switch_13,
  input  MUX___track_switch_14,
  input  MUX___track_switch_15,
  input  MUX___track_switch_16,
  input  [3:0] in_34,
  input  [3:0] in_35,
  input  [3:0] in_36,
  input  [3:0] in_37,
  input  [3:0] bus_input,
  input  in_39,
  input  in_40,
  input  in_41,
  output [3:0] out_42
);

  wire the_station_picker_2_d0, the_station_picker_2_d3, The_station_picker_d0, The_station_selector__MAR_o0,
       The_station_selector__MAR_o1, The_station_selector__MAR_o2, The_station_selector__MAR_o3;

  _4_bit_register The_station_selector__MAR (
    .i0(in_1), .i1(in_2), .i2(in_3), .i3(in_4), .enable(in_5), .set(in_5), .o0(The_station_selector__MAR_o0),
    .o1(The_station_selector__MAR_o1), .o2(The_station_selector__MAR_o2), .o3(The_station_selector__MAR_o3));
  decoder the_station_picker_2 (
    .A1(The_station_selector__MAR_o2), .A0(The_station_selector__MAR_o3), .D0(the_station_picker_2_d0),
    .D1(the_station_picker_2_d0), .D2(the_station_picker_2_d0), .D3(the_station_picker_2_d3));
  assign out_42 = in_39 ? bus_input : 4'bz;  // Controlled_Buffer controlled_buffer_1
  decoder The_station_picker (
    .A1(The_station_selector__MAR_o0), .A0(The_station_selector__MAR_o1), .D0(The_station_picker_d0),
    .D1(the_station_picker_2_d0), .D2(the_station_picker_2_d0), .D3(the_station_picker_2_d0));
  small_unit small_unit (
    .HW(the_station_picker_2_d0), .bus_controller(MUX___track_switch), .bus(out_42), .S(in_40), .E(in_41),
    .VW(the_station_picker_2_d0), .writing_to_the_register(in_10));
  small_unit small_unit_2 (
    .HW(the_station_picker_2_d0), .bus_controller(MUX___track_switch_5), .bus(out_42), .S(in_40), .E(in_41),
    .VW(the_station_picker_2_d0), .writing_to_the_register(in_18));
  small_unit small_unit_3 (
    .HW(the_station_picker_2_d0), .bus_controller(MUX___track_switch_9), .bus(out_42), .S(in_40), .E(in_41),
    .VW(the_station_picker_2_d0), .writing_to_the_register(in_26));
  small_unit small_unit_4 (
    .HW(the_station_picker_2_d3), .bus_controller(MUX___track_switch_13), .bus(out_42), .S(in_40), .E(in_41),
    .VW(the_station_picker_2_d0), .writing_to_the_register(in_34));
  small_unit small_unit_5 (
    .HW(the_station_picker_2_d0), .bus_controller(MUX___track_switch_2), .bus(out_42), .S(in_40), .E(in_41),
    .VW(the_station_picker_2_d0), .writing_to_the_register(in_11));
  small_unit small_unit_6 (
    .HW(the_station_picker_2_d0), .bus_controller(MUX___track_switch_6), .bus(out_42), .S(in_40), .E(in_41),
    .VW(the_station_picker_2_d0), .writing_to_the_register(in_19));
  small_unit small_unit_7 (
    .HW(the_station_picker_2_d0), .bus_controller(MUX___track_switch_10), .bus(out_42), .S(in_40), .E(in_41),
    .VW(the_station_picker_2_d0), .writing_to_the_register(in_27));
  small_unit small_unit_8 (
    .HW(the_station_picker_2_d3), .bus_controller(MUX___track_switch_14), .bus(out_42), .S(in_40), .E(in_41),
    .VW(the_station_picker_2_d0), .writing_to_the_register(in_35));
  small_unit small_unit_9 (
    .HW(the_station_picker_2_d0), .bus_controller(MUX___track_switch_3), .bus(out_42), .S(in_40), .E(in_41),
    .VW(the_station_picker_2_d0), .writing_to_the_register(in_12));
  small_unit small_unit_10 (
    .HW(the_station_picker_2_d0), .bus_controller(MUX___track_switch_7), .bus(out_42), .S(in_40), .E(in_41),
    .VW(the_station_picker_2_d0), .writing_to_the_register(in_20));
  small_unit small_unit_11 (
    .HW(the_station_picker_2_d0), .bus_controller(MUX___track_switch_11), .bus(out_42), .S(in_40), .E(in_41),
    .VW(the_station_picker_2_d0), .writing_to_the_register(in_28));
  small_unit small_unit_12 (
    .HW(the_station_picker_2_d3), .bus_controller(MUX___track_switch_15), .bus(out_42), .S(in_40), .E(in_41),
    .VW(the_station_picker_2_d0), .writing_to_the_register(in_36));
  small_unit small_unit_13 (
    .HW(the_station_picker_2_d0), .bus_controller(MUX___track_switch_4), .bus(out_42), .S(in_40), .E(in_41),
    .VW(The_station_picker_d0), .writing_to_the_register(in_13));
  small_unit small_unit_14 (
    .HW(the_station_picker_2_d0), .bus_controller(MUX___track_switch_8), .bus(out_42), .S(in_40), .E(in_41),
    .VW(The_station_picker_d0), .writing_to_the_register(in_21));
  small_unit small_unit_15 (
    .HW(the_station_picker_2_d0), .bus_controller(MUX___track_switch_12), .bus(out_42), .S(in_40), .E(in_41),
    .VW(The_station_picker_d0), .writing_to_the_register(in_29));
  small_unit small_unit_16 (
    .HW(the_station_picker_2_d3), .bus_controller(MUX___track_switch_16), .bus(out_42), .S(in_40), .E(in_41),
    .VW(The_station_picker_d0), .writing_to_the_register(in_37));

  // Notes on the sheet:
  //   turn the buffer on 
  //   if you want to write
  //   into the bus
  //   . The Station Selector (MAR):
  //   . The Station Pickers (2x4 Decoders):
  //   . Trying Another Station:
  //   . The Spotlight Turns On (AND1 in the Selected Unit):
  //   . Grabbing a Train from the Tracks (Writing Data):
  //   Let’s say we want to park a new train (like 1010) at Unit 0:
  //   . Sending a Train onto the Tracks (Reading Data):
  //   Now let’s send Unit 0’s train (1010) onto the tracks:
  //   . Keeping the Tracks Clear (Avoiding Chaos):
  //   The two 2x4 decoders are like two toy pickers working together to find the right station:
  //   . Put 1010 on the Data Bus (the tracks) using the Bus Input.
  //   . Keep the MAR at 0000, so Unit 0 is still selected (H0 and V0 are on).
  //   Let’s say we want to park a train (1111) at Unit 15 (the last station):
  //   . Turn “s” off (0), and Unit 0’s register now holds 1010—like parking a new train at the station!
  //   . Set the MAR to 1111, so the decoders turn on H3 and V3, selecting Unit 15.
  //   . Put 1111 on the Data Bus, set Select to 0, “s” to 1, and “e” to 0—Unit 15 saves 1111.
  //   . Set the Select bit to 0 for Unit 0’s MUX, so it connects the Data Bus to the register’s input (ready to grab the train).
  //   . Set the Select bit to 1 for Unit 0’s MUX, so it connects the register’s output to the Data Bus (ready to send the train).
  //   . To read it back, keep the MAR at 1111, set Select to 1, “s” to 0, and “e” to 1—the Bus Output shows 1111.
  //   Why It’s a 64-Bit RAM
  //   You’ve Got a 64-Bit RAM!
  //   The Big Picture: Components of the 64-Bit RAM
  //   How small units function is explained in details in the small unit crcuit
  //   Let’s imagine the entire 64-bit RAM in action, like a busy train station where trains are arriving and departing, but only one station is active at a time.
  //   . Look at the Bus Output—it shows 1010, like the train leaving the station and rolling onto the tracks for everyone to see!
  //   Step-by-Step Description: Building the 64-Bit RAM
  //   . 4-Bit Data Bus (The Train Tracks): This is the shared pathway that all 16 stations use to send and receive trains (data). It’s 4 bits wide, matching the size of the trains each station holds.
  //   . 4-Bit Memory Address Register (MAR, The Station Selector): This is a little box that holds a 4-bit address (a number from 0 to 15, since 2^4 = 16), telling the decoders which station to pick.
  //   How the 64-Bit RAM Works as a Whole
  //   . Together, they select one station. If H0 and V0 are on, they pick Unit 0 (at row 0, column 0). If H3 and V3 are on, they pick Unit 15 (at row 3, column 3).
  //   . The MAR is set to 0000, so the decoders turn on H0 and V0, selecting Unit 0. Unit 0’s AND1 output is 1, while all other units have AND1 output as 0.
  //   . Set “s” to 1 and “e” to 0. Since Unit 0 is selected, AND2’s output is 1 (AND1 is 1, “s” is 1), telling the register to save the data from the MUX (1010 from the bus).
  //   . Set “s” to 0 and “e” to 1. Since Unit 0 is selected, AND3’s output is 1 (AND1 is 1, “e” is 1), allowing the MUX to send the register’s data (1010) to the Data Bus.
  //   . 16 Small Units (Little Toy Stations): Each unit is a tiny station that can store a 4-bit value (like a train with 4 cars). There are 16 units total, arranged in a 4x4 grid, so they can store 64 bits altogether.
  //   . The first decoder (Horizontal) looks at the first 2 bits of the MAR (A1, A0) and picks one of 4 horizontal rows (H0, H1, H2, H3). For example, if A1A0 is 00, it turns on H0.
  //   . The second decoder (Vertical) looks at the other 2 bits of the MAR (A3, A2) and picks one of 4 vertical columns (V0, V1, V2, V3). For example, if A3A2 is 00, it turns on V0.
  //   . “s” (Set) and “e” (Enable) Bits (The Station Managers): These are two switches that manage what each station does: “s” tells a station to grab a new train from the tracks, and “e” tells it to send its train onto the tracks.
  //   Inside each small unit, the horizontal and vertical wires from the decoders go into AND1. Only the selected unit has both wires on (1), so its AND1 output is 1—like a spotlight shining on that station, saying, “You’re up!”
  //   . Two 2x4 Decoders (The Station Pickers): These are like two toy pickers that work together to choose one station out of the 16. One picker selects a row (horizontal), and the other selects a column (vertical), pinpointing exactly one station.
  //   . Multiplexer (MUX) in Each Unit (The Track Switch): Each station has a 4-bit 2-to-1 MUX that acts like a switch for the tracks: it decides whether the station grabs a train from the tracks (reading from the bus) or sends its train onto the tracks (writing to the bus).
  //   The MAR is like the station master holding a 4-bit ticket (a number from 0000 to 1111, or 0 to 15). This ticket tells the decoders which of the 16 stations to pick. For example, if the MAR holds 0000, it picks the first station (Unit 0); if it holds 1111, it picks the last station (Unit 15).
  //   The train station has 16 little stations (4x4 grid), and each station holds a 4-bit train. That’s 16 × 4 = 64 bits total, making this a 64-bit RAM. You can store 16 different 4-bit values (like 1010, 1111, etc.), and the MAR lets you pick any one of them randomly, just like the book’s 256-byte RAM but scaled down. It’s called Random Access Memory because you can access any station just as quickly as any other—no matter where it is in the grid, it’s always ready to go!
  //   Your 64-bit RAM is like a big toy train station with 16 little stations inside, arranged in a 4x4 grid (4 rows and 4 columns). Each little station can hold a 4-bit train (a 4-bit value), so together, the 16 stations store 64 bits (16 × 4 = 64). You can pick any one of these stations at a time to either park a new train (write data) or send its train onto the tracks (read data). It’s called Random Access Memory (RAM) because you can access any station just as quickly as any other, no matter where it is in the grid—super handy for a computer!
  //   Your 64-bit RAM is like a big toy train station with 16 little stations, each holding a 4-bit train, for a total of 64 bits. The 2x4 decoders act like toy pickers, selecting one station at a time with a 4-bit address from the MAR. Each station uses a MUX to switch between grabbing a train from the tracks (Data Bus) or sending its train onto the tracks, with the “s,” “e,” and Select bits managing the flow. It’s a perfect mini version of the 256-byte RAM from But How Does It Know?, and you’ve built half of a computer—amazing! Next time, we can explore the ALU or add more features
  //   The 2x4 decoders ensure only one small unit is selected at a time (only one AND1 output is 1). For all other units, AND1 is 0, so their AND2 and AND3 outputs are 0, meaning they don’t interact with the bus. Even if their Select bit is 1, they won’t send data because their “e” signal isn’t active (AND3 is 0). The MUX in each unit also helps by alternating the data flow: when Select is 0, the unit can only read from the bus; when Select is 1, it can only write to the bus. This keeps the tracks clear, with only one train moving at a time—no crashes!
endmodule

module small_unit (
  input  VW,
  input  HW,
  input  bus_controller,
  input  [3:0] writing_to_the_register,
  input  S,
  input  E,
  output [3:0] bus
);

  wire AND_1_out, AND_2_out, AND_3_out;
  wire [3:0] multiplexer_1_out;

  and AND_1 (AND_1_out, HW, VW);
  and AND_2 (AND_2_out, AND_1_out, S);
  and AND_3 (AND_3_out, AND_1_out, E);
  _4_bit_register u_4_bit_register_1 (
    .i0(multiplexer_1_out[0]), .i1(multiplexer_1_out[1]), .i2(multiplexer_1_out[2]),
    .i3(multiplexer_1_out[3]), .enable(AND_2_out), .set(AND_3_out), .o0(bus[0]), .o1(bus[1]), .o2(bus[2]),
    .o3(bus[3]));
  Multiplexer #(.width(4)) multiplexer_1 (
    .in0(bus), .in1(writing_to_the_register), .out(multiplexer_1_out), .sel(bus_controller));  // open: en

  // Notes on the sheet:
  //   The small unit has:
  //   . A 4-bit bus (the Data Bus) for I/O, shared by all units.
  //   Step 4: Avoiding Chaos
  //   . A 4-bit register to store 4 bits of data (like a tiny toy box).
  //   Step 1: The 4x16 Decoder Picks the Small Unit
  //   . A3 (the enabler E) decides which 3x8 decoder is active:
  //   . If E (A3) is 1, Decoder 2 is on, and it picks one of D8 to D15.
  //   Step 2: Writing to the Small Unit (Using the Multiplexer)
  //   Let’s say we want to write data from the bus (like 1010, which is 10):
  //   . Put 1010 on the Data Bus (using a 4-bit input pin).
  //   If you want to write from the writing input instead (let’s say 1111):
  //   . Put 1111 on the writing input (a separate 4-bit input pin).
  //   . Set “s” to 1 (with the unit selected), and the register saves 1111
  //   Step 3: Reading from the Small Unit (Sending to the Bus)
  //   How It Works
  //   . If E (A3) is 0, Decoder 1 is on (NOT E is 1), and it picks one of D0 to D7.
  //   . When the select bit is 0, the MUX lets the register read from the Data Bus.
  //   . Set the MUX select bit to 0, so the MUX connects the Data Bus to the register’s input.
  //   . Set the MUX select bit to 1, so the MUX connects the writing input to the register.
  //   To send the register’s data to the bus (like reading the 1010 we stored):
  //   Inside the Small Unit
  //   . Three AND gates to control the register’s set and enable inputs, ensuring only the selected unit can read from or write to the bus.
  //   How It Works Step by Step
  //   The small unit has a 4-bit 2-to-1 multiplexer (MUX) to control what data goes into the register. You’ve set it up so:
  //   . Turn “s” off (0), and the register holds onto 1010—like parking the train with 4 cars (1010) at the station!
  //   Scaling Down to Our 4x4 Grid
  //   . The 2x4 decoders select one of the 16 units using a 4-bit address (A3A2 for vertical, A1A0 for horizontal).
  //   . The selected unit uses its MUX to read from or write to the bus, controlled by the select bit, “s,” and “e.”
  //   . A multiplexer (MUX) to alternate the register’s input: when the select bit is 0, it reads from the bus; when the select bit is 1, it reads from a writing input.
  //   . A2, A1, and A0 tell the active decoder which output to turn on. For example, if A3A2A1A0 is 0111 (7), E is 0, so Decoder 1 turns on D7.
  //   . When the select bit is 1, the MUX lets the register read from a writing input (a separate 4-bit input for writing data directly).
  //   . The third AND gate (AND3) combines AND1’s output (1 if this unit is selected) with the “e” (enable) bit. If “e” is 1, AND3’s output is 1.
  //   In our 16-bit RAM, we’re using a 4x4 grid with two 2x4 decoders (not the full 4x16), so we have 16 small units. The process is the same:
  //   Let’s imagine we’re playing with a toy train set, where the small unit is a little station that can store 4 bits (a tiny train with 4 cars), and the 4x16 decoder is our toy picker choosing which station gets to play.
  //   . In our RAM’s 4x4 grid, the 2x4 decoders work similarly: A3A2 picks a vertical wire, A1A0 picks a horizontal wire, selecting one of the 4 units.
  //   . Since you’re using the MUX to handle both reading and writing, set the MUX select bit to 1. This connects the register’s 4-bit output to the Data Bus through the MUX.
  //   Inside the small unit, the horizontal and vertical grid wires (from the decoders) go into the first AND gate (AND1). If both wires are 1, AND1’s output is 1, meaning this unit is selected—like shining a spotlight on this toy station!
  //   . The second AND gate (AND2) combines AND1’s output (1 if this unit is selected) with the “s” (set) bit. If “s” is 1, AND2’s output is 1, and the register saves the data from the MUX (which is 1010 from the bus).
  //   The 4x16 decoder (or our 2x4 decoders in the RAM) uses the 4-bit input A3A2A1A0 to pick one small unit. In our RAM, we have a 4x4 grid (4 units total), but let’s pretend we’re using the full 4x16 decoder setup with 16 units (we can scale it down later).
  //   . When AND3’s output is 1 (meaning the unit is selected and “e” is 1), the MUX sends the register’s data (1010) to the Data Bus. You can see this on a 4-bit output pin connected to the bus—like sending the train out of the station to show everyone its 4 cars!
  //   Each small unit is like a little toy box at an intersection of the grid, holding 4 bits of data (since we’re using 4-bit registers for our 16-bit RAM). The 4x16 decoder (or our 2x4 decoders in the RAM) picks which small unit gets to play by turning on one horizontal and one vertical grid wire. Let’s see how the small unit uses this selection, along with your multiplexer, to read and write data.
  //   . The MUX ensures that only one direction of data flow happens at a time: when the select bit is 0, the register reads from the bus; when it’s 1, the register writes to the bus. This prevents collisions without needing controlled buffers, as long as only one unit’s MUX is active at a time (which the decoder ensures).
  //   Since all 4 small units (or 16 if we used the full 4x16 decoder) share the same Data Bus, we need to make sure only one unit sends data at a time. The 4x16 decoder ensures only one unit is selected (only one AND1 output is 1), and the MUX’s select bit ensures the data flow is controlled. When the select bit is 1 for the selected unit, it sends data to the bus; all other units should have their select bit set to 0 (or their AND3 output off), so they don’t interfere. It’s like making sure only one toy station sends its train onto the tracks at a time—no crashes!
endmodule

module _4_bit_register (
  input  i0,
  input  i1,
  input  i2,
  input  i3,
  input  enable,
  input  set,
  output o0,
  output o1,
  output o2,
  output o3
);

  wire and_1_out, and_2_out, and_3_out, and_4_out;

  and and_1 (and_1_out, i0, enable);
  and and_2 (and_2_out, i1, enable);
  and and_3 (and_3_out, i2, enable);
  and and_4 (and_4_out, i3, enable);
  a_bit_of_memory a_bit_of_memory_1 (.i(and_1_out), .s(set), .o(o0));
  a_bit_of_memory a_bit_of_memory_2 (.i(and_2_out), .s(set), .o(o1));
  a_bit_of_memory a_bit_of_memory_3 (.i(and_3_out), .s(set), .o(o2));
  a_bit_of_memory a_bit_of_memory_4 (.i(and_4_out), .s(set), .o(o3));

  // Notes on the sheet:
  //   Enabler
  //   A bit of memory
  //   A bit of memory
  //   A bit of memory
  //   A bit of memory
  //   We used a 4-bit register in the register circuit because it aligns with the 4-bit Data Bus, enabling efficient data transfer,
  //   and it allows the 16 small units to collectively store 64 bits (16 × 4), simplifying the design while meeting our storage needs.
endmodule

module built_in_RAM_component (
  input  [7:0] in_1,
  input  [7:0] in_2,
  input  in_3,
  input  in_4
);

  wire clock_1_out;

  Clock clock_1 (.out(clock_1_out));
  RAM ram_1 (.addr(in_1), .data(in_2), .clk(clock_1_out), .ld(in_3), .clr(in_4));  // open: sel

  // Notes on the sheet:
  //   Key Parts of the Built-In RAM
  //   Extra Features of the Built-In RAM
  //   A Day at the Magical Station
  //   The built-in RAM does the same job as our custom 64-bit RAM, but it’s much more efficient:
  //   The built-in RAM has some bonus features that make it even more practical:
  //   What Is the Built-In RAM?
  //   Let’s break down the RAM component by looking at its pins and settings, as if we’re exploring the control panel of our magical train station:
  //   How It’s Like Our Custom RAM (But Better!)
  //   . Simplicity: It’s all in one component—no need to build a grid of small units, decoders, or multiplexers. You just connect the pins and go!
  //   . Clock Synchronization: The Clock ensures writes only happen on a tick, which is great for keeping your computer’s operations in sync as you build the second half.
  //   . Scalability: You can easily change the Address Bits and Data Bits to make the RAM bigger (e.g., 8 bits per location or 256 locations) without rewiring everything.
  //   . Selecting a Location: In our custom RAM, we used two 2x4 decoders to create a 4x4 grid and select one of 16 small units. The built-in RAM does this internally with the Address pins—no decoders needed!
  //   . Reading Data: In our custom RAM, we used the “e” bit and the MUX (with Select = 1) to send the selected unit’s data to the bus. The built-in RAM uses the Output Enable (OE) pin to put the data on the Data Out pins.
  //   . Data Out (Q): This is the exit where trains leave the station. It’s a set of output pins that show the data stored at the selected platform. When you read from the RAM, the data at the chosen address appears here.
  //   . Write Enable (WE): This is a switch that decides whether to park a new train (write data). When WE is 1, the RAM saves the data from Data In to the selected address. When WE is 0, it only reads (or does nothing if not reading).
  //   Later, you tell the station master to pick platform 5 again, flip the “send” switch (OE = 1), and the train (1100) rolls out through the exit (Data Out) onto the tracks. It’s fast, organized, and ready for any train you send its way!
  //   . Clock (CLK): This is like the station’s clock, ticking to keep everything in sync. The built-in RAM only writes data on a clock tick (when the clock goes from 0 to 1), which helps keep operations orderly, especially in a bigger computer, we will build one later .
  //   . Keeping It Safe: In our custom RAM, the decoders and MUX ensured only one unit interacted with the bus at a time. The built-in RAM handles this internally, so there’s no risk of collisions—you don’t need to worry about managing multiple units or buffers.
  //   . Output Enable (OE): This is a switch that decides whether to send a train onto the tracks (read data). When OE is 1, the RAM puts the data at the selected address on the Data Out pins. When OE is 0, the Data Out pins are disabled (they don’t output anything).
  //   . Writing Data: In our custom RAM, we used the “s” bit and a MUX (with Select = 0) to write data from the bus to the selected unit’s register. The built-in RAM uses the Write Enable (WE) pin and the Clock to do the same thing, saving the data at the selected address.
  //   . Data In (D): This is the entrance to the station where new trains arrive. It’s a set of input pins where you send the data you want to store. For our 64-bit RAM, we’ll set the “Data Bits” to 4 (since each small unit in our custom RAM held 4 bits), but the built-in RAM can handle any width you choose.
  //   . Address (A): This is like the station master’s ticket, telling the RAM which platform to access. The address is a number that picks one of the storage locations. Since our custom RAM had 16 locations (4x4 grid), we need 4 bits for the address (2^4 = 16). In the built-in RAM, you set the “Address Bits” to 4 to match this.
  //   Imagine the built-in RAM as a magical train station with 16 platforms, each holding a 4-bit train. The station master (Address) picks a platform, like platform 5 (address 0101). You send a new train (1100) through the entrance (Data In), flip the “park” switch (WE = 1), and when the clock ticks, the train parks on platform 5.
  //   The built-in RAM in Logisim (found under the “Memory” library) is like a big, magical toy train station with lots of little platforms inside, each holding a train (a piece of data). You can pick any platform to park a new train (write data) or send its train onto the tracks (read data). It’s called Random Access Memory (RAM) because you can access any platform just as quickly as any other, no matter where it is in the station.
endmodule

module built_in_Register (
  input  [7:0] in_1,
  input  in_2,
  input  in_3,
  output [7:0] out_4
);

  Register_part register_1 (.D(in_1), .Q(out_4), .clk(in_3), .clr(in_2));  // open: en

  // Notes on the sheet:
  //   Key Features of a Built-In Register
  //   . Data In (D): The input where you send the new train (e.g., 1010) to store.
  //   How Built-In Registers in Logisim Work
  //   . Data Out (Q): The output that shows the train currently in the box (e.g., 1010).
  //   How It Works
  //   Why It’s Useful for Us
  //   . Data Width: You can set how many bits the register holds (e.g., 4 bits for our 4-bit trains), matching our project’s data width.
  //   . Clear (CLR): A reset button that clears the register to 0 (e.g., 0000 for a 4-bit register) when set to 1, regardless of the clock or Enable. It’s like emptying the toy box instantly!
  //   . Enable (E): A switch that decides if the clock’s tick is effective. When Enable is 1, the clock tick updates the register (like our old enable/set combo). When Enable is 0, the clock tick is ignored, and the register holds its current value—no update happens.
  //   A built-in register in Logisim (found under the “Memory” library) is like a tiny toy box that holds a small piece of data—like a 4-bit train—and keeps it safe until you need it! It can store a value (e.g., 1010), update it with a new value, and show the stored value on its output, all while syncing with a clock to keep things orderly
  //   Imagine a toy box with a 4-bit train inside (say, 1010). You put a new train (1100) at the entrance (Data In), flip the “save” switch (WE = 1), and when the clock ticks, the box swaps out the old train for the new one—now it holds 1100! The output (Data Out) always shows what’s in the box, and the clock ensures updates happen at the right time.
  //   . Clock (CLK): The heartbeat that acts like the enable/set mechanism we used in our custom register. The register only updates its value (saves Data In to Data Out) when the clock ticks (0 to 1) and the Enable pin is 1—think of the clock as a special case of our old enable/set signals, controlling when the update happens.
  //   The built-in register is perfect for the second half of your computer because it’s a simple, reliable way to store small pieces of data—like the 4-bit values we’re working with—without building everything from scratch. It’ll be great for holding temporary results in the ALU or managing the program counter, and it syncs with the clock we going to build later!
endmodule
