// Logisim project second half of the computer.circ as structural Verilog
module Right_shifter (
  input  shift_in,
  input  se_2,
  input  [7:0] \input ,
  input  se_1,
  output [7:0] \output ,
  output shift_out
);

  wire [6:0] register_1_q;

  Register register_1 (.D(\input ), .Q({shift_out, register_1_q}), .clk(se_1));  // open: en, clr
  Register register_2 (.D({register_1_q, shift_in}), .Q(\output ), .clk(se_2));  // open: en, clr

  // Notes on the sheet:
  //   It’s used for dividing numbers by 2 (e.g., 10101010, which is 170, becomes 01010101, which is 85) and for bit manipulation in programming.
  //   8-Bit Right Shifter
  //   An 8-bit right shifter is like a toy train with 8 cars (bits) on a track, sliding all the cars one spot to the right! If the input is 10101010, a right shift moves each bit one position right, turning 10101010 into 01010101—the rightmost bit (0) falls off, and a 0 is added on the left.
endmodule

module Left_shifter (
  input  se_2,
  input  [7:0] \input ,
  input  shift_in,
  input  se_1,
  output shift_out,
  output [7:0] \output 
);

  wire [7:1] register_1_q;

  Register register_1 (.D(\input ), .Q({register_1_q, shift_out}), .clk(se_1));  // open: en, clr
  Register register_2 (.D({shift_in, register_1_q}), .Q(\output ), .clk(se_2));  // open: en, clr

  // Notes on the sheet:
  //   8-Bit Left Shifter
  //   An 8-bit left shifter is like that same toy train, but sliding all 8 cars one spot to the left! So, 10101010 becomes 01010100—the leftmost bit (1) falls off, and a 0 is added on the right. It’s used for multiplying numbers by 2 (e.g., 10101010, which is 170, becomes 01010100, which is 84 in 8 bits due to overflow) and aligning bits in data processing.
endmodule

module Half_adder (
  input  a,
  input  b,
  output sum,
  output carry
);

  xor xor_1 (sum, a, b);
  and and_1 (carry, a, b);

  // Notes on the sheet:
  //   For example, if A = 1 and B = 1, C = 1; otherwise, C = 0.
  //   A half adder doesn’t handle a carry-in from a previous bit, so it’s only part of the story.
  //   For example, if A = 1 and B = 0, S = 1; if A = 1 and B = 1, S = 0.
  //   . Sum (S): The sum is 1 if exactly one car fits (A or B, but not both). This is an XOR operation: S = A XOR B.
  //   . Carry (C): The carry is 1 if both cars try to fit (A and B are both 1). This is an AND operation: C = A AND B.
  //   How it works
  //   A half adder is like a tiny toy calculator that adds two 1-bit numbers (A and B) and gives a 1-bit sum (S) and a 1-bit carry (C). Imagine two toy cars (A and B) trying to fit on one parking spot:
endmodule

module Full_adder (
  input  a,
  input  b,
  input  carry_in,
  output sum,
  output carry_out
);

  wire and_1_out, and_2_out, xor_1_out;

  xor xor_1 (xor_1_out, a, b);
  and and_1 (and_1_out, carry_in, xor_1_out);
  and and_2 (and_2_out, a, b);
  xor xor_2 (sum, xor_1_out, carry_in);
  or or_1 (carry_out, and_1_out, and_2_out);

  // Notes on the sheet:
  //   For example, if A = 1, B = 1, Cin = 0, Cout = 1 (from A AND B).
  //   For example, if A = 1, B = 1, Cin = 0, then S = 0 (1 + 1 + 0 = 10 in binary).
  //   . Sum (S): The sum is 1 if an odd number of inputs (A, B, Cin) are 1. This is an XOR of all three: S = A XOR B XOR Cin.
  //   . Carry-Out (Cout): The carry-out is 1 if at least two inputs are 1. This is: Cout = (A AND B) OR (A AND Cin) OR (B AND Cin).
  //   How it works
  //   A full adder is crucial because it’s like a super toy calculator that adds three bits at once—A, B, and a carry-in—making it possible to chain them together for adding big numbers like in our 8-bit adder, without missing any carryovers
  //   A full adder is like a bigger toy calculator that adds three 1-bit numbers: A, B, and a carry-in (Cin) from a previous addition, producing a 1-bit sum (S) and a 1-bit carry-out (Cout). It’s what we need for an 8-bit adder, where each bit position needs to handle a carry from the previous bit.
endmodule

module comparator (
  input  in_1,
  input  a__larger,
  input  a,
  input  b,
  output c,
  output all_bits_equal_so_far,
  output a__larger_2
);

  wire _2_out, _4_out;

  xor _1 (c, a, b);
  not _2 (_2_out, c);
  and _3 (all_bits_equal_so_far, _2_out, in_1);
  and _4 (_4_out, in_1, a, c);
  or _5 (a__larger_2, _4_out, a__larger);

  // Notes on the sheet:
  //   Function:
  //   Inputs:
  //   Outputs:
  //   . Bits a and b (the bits being compared).
  //   A single bit comparator is a circuit that compares two bits, a and b
  //   . “All bits above are equal” (1 if higher bits match; a constant 1 for the top unit).
  //   . “Equal”: From a NOT-XOR gate, outputs 1 if a = b, showing the bits match.
  //   unequal
  //   equal
  //   . “A larger from above” (1 if ‘a’ is already determined to be larger; a constant 0 for the top unit).
  //   . ‘c’: From an XOR gate (a XOR b), outputs 1 if a ≠ b, indicating a difference at this position.
  //   The outputs are passed to the next unit to continue the comparison, helping comparing 16 bits.
  //   all bits above are equal
  //   How it works
  //   . “A larger”: Outputs 1 if a = 1, b = 0 (a is larger, and 0 if a is smaller than b), and all higher bits are equal (computed by ANDing a[i], the XOR output, and the “all bits above are equal” input).
endmodule

module _8_bit_comparator (
  input  in_1,
  input  _128,
  input  _64,
  input  _32,
  input  _16,
  input  _8,
  input  _4,
  input  _2,
  input  _1,
  input  _128_2,
  input  _64_2,
  input  _32_2,
  input  _16_2,
  input  _8_2,
  input  _4_2,
  input  _2_2,
  input  _1_2,
  output out_18,
  output out_19,
  output out_20,
  output c,
  output out_22,
  output out_23,
  output out_24,
  output out_25,
  output equal,
  output a__larger
);

  wire comparator_1_a__larger_2, comparator_1_all_bits_equal_so_far, comparator_2_a__larger_2,
       comparator_2_all_bits_equal_so_far, comparator_3_a__larger_2, comparator_3_all_bits_equal_so_far,
       comparator_4_a__larger_2, comparator_4_all_bits_equal_so_far, comparator_5_a__larger_2,
       comparator_5_all_bits_equal_so_far, comparator_6_a__larger_2, comparator_6_all_bits_equal_so_far,
       comparator_7_a__larger_2, comparator_7_all_bits_equal_so_far;

  comparator comparator_1 (
    .a(_128), .b(_128_2), .in_1(1'b1), .a__larger(in_1),
    .all_bits_equal_so_far(comparator_1_all_bits_equal_so_far), .a__larger_2(comparator_1_a__larger_2),
    .c(out_18));
  comparator comparator_2 (
    .a(_64), .b(_64_2), .in_1(comparator_1_all_bits_equal_so_far), .a__larger(comparator_1_a__larger_2),
    .all_bits_equal_so_far(comparator_2_all_bits_equal_so_far), .a__larger_2(comparator_2_a__larger_2),
    .c(out_19));
  comparator comparator_3 (
    .a(_32), .b(_32_2), .in_1(comparator_2_all_bits_equal_so_far), .a__larger(comparator_2_a__larger_2),
    .all_bits_equal_so_far(comparator_3_all_bits_equal_so_far), .a__larger_2(comparator_3_a__larger_2),
    .c(out_20));
  comparator comparator_4 (
    .a(_16), .b(_16_2), .in_1(comparator_3_all_bits_equal_so_far), .a__larger(comparator_3_a__larger_2),
    .all_bits_equal_so_far(comparator_4_all_bits_equal_so_far), .a__larger_2(comparator_4_a__larger_2), .c(c));
  comparator comparator_5 (
    .a(_8), .b(_8_2), .in_1(comparator_4_all_bits_equal_so_far), .a__larger(comparator_4_a__larger_2),
    .all_bits_equal_so_far(comparator_5_all_bits_equal_so_far), .a__larger_2(comparator_5_a__larger_2),
    .c(out_22));
  comparator comparator_6 (
    .a(_4), .b(_4_2), .in_1(comparator_5_all_bits_equal_so_far), .a__larger(comparator_5_a__larger_2),
    .all_bits_equal_so_far(comparator_6_all_bits_equal_so_far), .a__larger_2(comparator_6_a__larger_2),
    .c(out_23));
  comparator comparator_7 (
    .a(_2), .b(_2_2), .in_1(comparator_6_all_bits_equal_so_far), .a__larger(comparator_6_a__larger_2),
    .all_bits_equal_so_far(comparator_7_all_bits_equal_so_far), .a__larger_2(comparator_7_a__larger_2),
    .c(out_24));
  comparator comparator_8 (
    .a(_1), .b(_1_2), .in_1(comparator_7_all_bits_equal_so_far), .a__larger(comparator_7_a__larger_2),
    .all_bits_equal_so_far(equal), .a__larger_2(a__larger), .c(out_25));
  comparator comparator_9 ();  // open: a, b, in_1, a__larger, all_bits_equal_so_far, a__larger_2, c

  // Notes on the sheet:
  //   Inputs:
  //   Outputs:
  //   Function:
  //   Example:
  //   . ‘a’ = 128+64+1 (11000001, 193), ‘b’ = 10101010 (170).
  //   . Bits a[i] and b[i] (e.g., a[7] and b[7] for the top unit).
  //   . Contributes to the final “equal” and “a larger” outputs.
  //   a
  //   b
  //   . c’: From an XOR gate (a[i] XOR b[i]), outputs 1 if bits differ, used for zero detection or difference checking.
  //   . “Equal”: Outputs 1 if all bits match (computed by ANDing all “equal” outputs from each unit), meaning ‘a’ = ‘b’.
  //   . At bit 6: a[6] = 1, b[6] = 0, bit 7 matches, so “a larger” is 1, “equal” is 0, and ‘c’ at bit 6 is 1 (bits differ).
  //   How it works
  //   . “All bits above are equal” and “a larger from above” signals from the previous unit (or constants for the top unit).
  //   . “A larger”: Outputs 1 if ‘a’ > ‘b’ (determined by the first unit where a[i] = 1, b[i] = 0, and higher bits are equal, propagated through OR gates).
  //   Approach: The Comparator as an Enigma Codebreaker
  //   An 8-bit comparator compares two 8-bit inputs, ‘a[i]’ and ‘b[i]’ (16 bits total), using 8 single bit comparators stacked from bit 7 (most significant) to bit 0 (least significant), functioning like a complete Enigma machine deciphering two 8-bit messages.
  //   Imagine the 8-bit comparator as a World War II Enigma machine, used by codebreakers like Alan Turing to decipher enemy messages. Each single bit comparator is like a rotor in the Enigma, analyzing one pair of letters (bits a[i] and b[i]) in a coded message.
  //   The static 1 and 0 at the top are the initial settings of the machine, starting the decoding process. The full 8-bit comparator, with its 8 rotors, deciphers the entire message (‘a’ vs. ‘b’), outputting whether the codes are identical (“equal”) or if one is greater (“a larger”), just like breaking an 8-letter Enigma code to reveal a hidden instruction.
  //   The rotor’s job is to check if the letters match (‘c’ output: 1 if they differ, like spotting a mismatch in the code), if they’re the same (“equal” output: 1 if a[i] = b[i], like confirming a correct letter pair), and if one letter is “larger” (a[i] = 1, b[i] = 0, like determining which code has a higher value at this position). The “all bits above are equal” signal is like a codebreaker’s log, ensuring all previous letters matched before deciding which code is “larger.”
endmodule

module ALU (
  input  [7:0] a,
  input  [7:0] b,
  input  carry_in,
  input  should_be_always_0,
  input  [2:0] op_code,
  output zero,
  output [7:0] out_7,
  output carry_out,
  output a__larger,
  output equal
);

  wire and_2_out, and_3_out, decoder_1_out0, decoder_1_out1, decoder_1_out2, decoder_1_out3, decoder_1_out4,
       decoder_1_out5, decoder_1_out6, Lclk_out, or_2_out, Rclk_out, SHL_shift_out, SHR_shift_out;
  wire [7:0] ADD_out_18, and_1_out, not_1_out, or_1_out, SHL_output, SHR_output, xor_1_out;

  assign xor_1_out = a ^ b;  // XOR_Gate xor_1, 8 bits wide
  assign or_1_out = a | b;  // OR_Gate or_1, 8 bits wide
  assign and_1_out = a & b;  // AND_Gate and_1, 8 bits wide
  assign not_1_out = ~b;  // NOT_Gate not_1, 8 bits wide
  Left_shifter SHL (
    .\input (a), .shift_in(carry_in), .se_1(and_2_out), .se_2(and_2_out), .shift_out(SHL_shift_out),
    .\output (SHL_output));
  and and_2 (and_2_out, Lclk_out, decoder_1_out4);
  Right_shifter SHR (
    .shift_in(carry_in), .\input (a), .se_1(and_3_out), .se_2(and_3_out), .\output (SHR_output),
    .shift_out(SHR_shift_out));
  Clock Rclk (.out(Rclk_out));
  and and_3 (and_3_out, Rclk_out, decoder_1_out5);
  _8_bit_comparator ADD (
    ._128(a[7]), ._64(a[6]), ._32(a[5]), ._16(a[4]), ._8(a[3]), ._4(a[2]), ._2(a[1]), ._1(a[0]),
    ._128_2(b[7]), ._64_2(b[6]), ._32_2(b[5]), ._16_2(b[4]), ._8_2(b[3]), ._4_2(b[2]), ._2_2(b[1]),
    ._1_2(b[0]), .in_1(should_be_always_0), .equal(equal), .a__larger(a__larger), .out_18(ADD_out_18[0]),
    .out_19(ADD_out_18[1]), .out_20(ADD_out_18[2]), .c(ADD_out_18[3]), .out_22(ADD_out_18[4]),
    .out_23(ADD_out_18[5]), .out_24(ADD_out_18[6]), .out_25(ADD_out_18[7]));
  Clock Lclk (.out(Lclk_out));
  Decoder #(.select(3)) decoder_1 (
    .out0(decoder_1_out0), .out1(decoder_1_out1), .out2(decoder_1_out2), .out3(decoder_1_out3),
    .out4(decoder_1_out4), .out5(decoder_1_out5), .out6(decoder_1_out6), .sel(op_code));  // open: out7, en
  assign out_7 = decoder_1_out0 ? xor_1_out : 8'bz;  // Controlled_Buffer controlled_buffer_1
  assign out_7 = decoder_1_out1 ? or_1_out : 8'bz;  // Controlled_Buffer controlled_buffer_2
  assign out_7 = decoder_1_out2 ? and_1_out : 8'bz;  // Controlled_Buffer controlled_buffer_3
  assign out_7 = decoder_1_out3 ? not_1_out : 8'bz;  // Controlled_Buffer controlled_buffer_4
  assign out_7 = decoder_1_out4 ? SHL_output : 8'bz;  // Controlled_Buffer controlled_buffer_5
  assign out_7 = decoder_1_out5 ? SHR_output : 8'bz;  // Controlled_Buffer controlled_buffer_6
  assign out_7 = decoder_1_out6 ? ADD_out_18 : 8'bz;  // Controlled_Buffer controlled_buffer_7
  not not_2 (zero, or_2_out);
  or or_2 (or_2_out, out_7[0], out_7[1], out_7[2], out_7[3], out_7[4], out_7[5], out_7[6], out_7[7]);
  or or_3 (carry_out, SHL_shift_out, SHR_shift_out);

  // Notes on the sheet:
  //   7 Tools:
  //   . AND: Checks where ‘a’ and ‘b’ both have 1s.
  //   . NOT: Flips ‘a’ (turns 1s to 0s and 0s to 1s).
  //   How It Works
  //   Why It’s Cool
  //   It has 7 tools inside, and you pick one tool at a time to use!
  //   . XOR: Mixes ‘a’ and ‘b’ in a special way (like a secret code).
  //   . OR: Combines ‘a’ and ‘b’ (if either has a 1, the result gets a 1).
  //   . SHL: Slides ‘a’ left by 1 spot (like 10101010 becomes 01010100).
  //   . SHR: Slides ‘a’ right by 1 spot (like 10101010 becomes 01010101).
  //   . Comparator: Tells if ‘a’ is bigger than ‘b’ or if they’re the same.
  //   . A decoder (like a tool selector) turns on one tool using the “op” code.
  //   . The tool’s 8-bit result goes to the “Result” output, but only one tool works at a time!
  //   . You give it ‘a’, ‘b’, a “Carry In” bit, and a 3-bit “op” code to pick the tool (like 000 for XOR, 100 for SHL).
  //   Approach :The ALU is a Toolbox!
  //   What’s Inside the Toolbox?
  //   . Extra outputs: “Zero” (lights up if Result is 00000000), “A Larger” (lights up if ‘a’ is bigger), and “Equal” (lights up if ‘a’ equals ‘b’).
  //   Think of the ALU as a magical toolbox that helps your computer do math and logic stuff with two 8-bit numbers, ‘a’ and ‘b’ (like 10101010 and 11001100).
  //   The ALU is your computer’s handyman, doing all the math and comparing jobs, and the clock makes sure SHL and SHR work at the right time!
  //   . SHL and SHR have little storage boxes (registers) that save their inputs and outputs, and they only work when a clock (clk) says “go” (clk = 1). We’ll explain the clock next chapter—it’s like a timer that keeps everything in sync!
endmodule

module bus_1 (
  input  MSB,
  input  in_2,
  input  in_3,
  input  in_4,
  input  in_5,
  input  in_6,
  input  in_7,
  input  LSB,
  input  bus_1,
  output [7:0] Output
);

  wire not_1_out;

  and and_1 (Output[7], MSB, not_1_out);
  and and_2 (Output[6], in_2, not_1_out);
  and and_3 (Output[5], in_3, not_1_out);
  and and_4 (Output[3], in_5, not_1_out);
  and and_5 (Output[4], in_4, not_1_out);
  and and_6 (Output[2], in_6, not_1_out);
  and and_7 (Output[1], in_7, not_1_out);
  not not_1 (not_1_out, bus_1);
  or or_1 (Output[0], LSB, bus_1);

  // Notes on the sheet:
  //   What is this bus 1 useful for?
  //   As the name indicates The "bus 1" is a special 8-bit register that outputs the binary value 00000001 (decimal 1) when its enable input (bus 1 input) is 1 and the bus input is 0. When enabled, it places the value 1 onto the bus, allowing the ALU to add 1 to another value on the bus, such as the Instruction Address Register (IAR). This is particularly useful during the fetch cycle to increment IAR, pointing to the next instruction in RAM.
endmodule

// clk d
module clock (
  input  clk,
  input  clk_2,
  input  clk_3,
  input  clk_4,
  input  clk_5,
  output clk_e,
  output clk_s,
  output out_8
);

  not not_1 (clk_2, clk_2);
  not not_2 (clk_4, clk_4);
  not not_3 (clk, clk);
  Clock clock_1 (.out(out_8));
  or or_1 (clk_e, clk_4, clk_4);
  and and_1 (clk_s, clk_4, clk_4);

  assign clk_3 = clk_2;
  assign clk_5 = clk_4;

  // Notes on the sheet:
  //   Note for better understanding
  //   https://github.com/hossamIII/But-How-Do-it-Know--logisim-version-.git
  //   How it works
  //   To slow it down, you add a longer wire or use a resistor (delaying the signal by about a quarter of a cycle):
  //   It’s made by connecting a NOT gate’s output back to its input, creating a loop that keeps flipping the bit (1 → 0 → 1 → 0 …):
  //   . The clock sets the pace for the whole computer, like a drummer keeping the beat.
  //   . Add the Clock: Go to the “Wiring” library in Logisim, pick the “Clock” component, and place it in your circuit.
  //   This PDF explains the clock’s role as the computer’s heartbeat and includes diagrams to show how it ticks over time.
  //   Now we're going to do something fairly simple. We will take the original clock and the delayed clock, and both AND them and OR them to create two new bits, like so:
  //   To gain a deeper understanding of the clock signals (clk e and clk s) and visualize how they work, we recommend visiting the "clock.pdf" document located in the project repository at
  //   . Set the Ticks: Double-click the Clock to set its timing. “High Duration” is how long it’s on (1), and “Low Duration” is how long it’s off (0). For example, set both to 1 tick for a simple 0, 1, 0, 1 pattern.
  //   . Make It Work: To see the clock in action, press Ctrl+K (or go to Simulate → Ticks Enabled). This starts the ticks, and the clock will flip between 0 and 1 automatically during the simulation.
  //   . The clock’s job is to time when data moves: first, enable a “from” register to send data on the bus, then enable a “to” register to capture it, ensuring the “to” register grabs the data before the “from” register turns off.
  //   . clk e (from the OR): This signal turns on first and stays on longer. It’s like opening a gate to let the first storage box put its number onto the bus, giving the number plenty of time to travel.
  //   These three circuits are just to explain how a clock works—we don’t need to build them in Logisim. Logisim has a built-in Clock component that already gives us a clock signal (0, 1, 0, 1 …), so we’ll use that instead to save time and keep things simple.
  //   . Why This Timing Matters: Since clk e stays on longer, the number is ready on the bus when clk s turns on. This makes sure the second storage box gets the correct number before the first storage box stops sending it, avoiding any mistakes.
  //   The clock is a bit that flips between on (1) and off (0) super fast :billions of times per second, or gigahertz ( it was decided to use a name of a nerd scientist who lived in Germany who did some of the early research in 1800's that led up to radio to use his name to describe how fast electricity was going on and off persecond )setting the timing for the whole computer.
  //   . clk s (from the AND): This signal turns on later, right in the middle of when clk e is on, and it’s on for a shorter time. It’s like opening a second gate to let another storage box grab the number from the bus and save it, but only after the number has had time to arrive safely.
  //   The third circuit is really helpful because it makes two special signals—clk e and clk s—that work together to move data safely inside the computer. Imagine the computer has little storage boxes (we’ll call them storage boxes for now) that hold numbers, like 10101010. We need to move a number from one storage box to another through a shared path called the bus, but we have to make sure the number doesn’t get mixed up or lost.
endmodule

module clock_we_gonna_use (
  output clk,
  output clk_e,
  output clk_s
);

  wire clk_d_out;

  Clock #(.highDuration(2)) u_clk (.out(clk));
  Clock clk_d (.out(clk_d_out));
  or or_1 (clk_e, clk, clk_d_out);
  and and_1 (clk_s, clk, clk_d_out);

  // Notes on the sheet:
  //   1 tick on high/low
  //   2 ticks on high
  //   Ticks and Clock Speed:
  //   . The Clock component has two settings: “High Duration” (how many ticks the clock is on, or 1) and “Low Duration” (how many ticks it’s off, or 0).
  //   . It’s In Logisim, a “tick” is like a tiny step in the simulation—it’s how time moves forward. by connecting a NOT gate’s output back to its input, creating a loop that keeps flipping the bit (1 → 0 → 1 → 0 …):
  //   . If you make the High Duration longer (more ticks), the clock stays on longer, which slows down the overall on-off cycle. For example, High Duration of 2 ticks and Low Duration of 1 tick means the clock is on for 2 ticks, off for 1 tick, repeating every 3 ticks—slower than 1 tick on, 1 tick off.
endmodule

module _1_bit_memory (
  input  in_1,
  input  in_2,
  output out_3
);

  wire nand_1_out, nand_2_out, nand_4_out;

  nand nand_1 (nand_1_out, in_1, in_2);
  nand nand_2 (nand_2_out, nand_1_out, in_2);
  nand nand_3 (out_3, nand_1_out, nand_4_out);
  nand nand_4 (nand_4_out, out_3, nand_2_out);
endmodule

module Stepper (
  input  reset,
  input  in_2,
  output step_1,
  output step_2,
  output step_3,
  output step_4,
  output step_5,
  output step_6,
  output step_7
);

  wire _1_bit_memory_2_out_3, _1_bit_memory_3_out_3, _1_bit_memory_4_out_3, _1_bit_memory_5_out_3,
       _1_bit_memory_6_out_3, _1_bit_memory_7_out_3, _1_bit_memory_8_out_3, _1_bit_memory_9_out_3,
       _1_bit_memory_10_out_3, _1_bit_memory_11_out_3, _1_bit_memory_out_3, not_1_out, not_2_out, not_3_out,
       not_4_out, not_5_out, not_6_out, not_7_out, not_8_out, or_2_out, or_3_out;

  not not_1 (not_1_out, in_2);
  or or_1 (step_1, reset, not_3_out);
  not not_2 (not_2_out, reset);
  or or_2 (or_2_out, reset, not_1_out);
  or or_3 (or_3_out, reset, in_2);
  not not_3 (not_3_out, _1_bit_memory_2_out_3);
  _1_bit_memory _1_bit_memory (.in_1(not_2_out), .in_2(or_2_out), .out_3(_1_bit_memory_out_3));
  _1_bit_memory _1_bit_memory_2 (.in_1(_1_bit_memory_out_3), .in_2(or_3_out), .out_3(_1_bit_memory_2_out_3));
  and and_1 (step_2, _1_bit_memory_2_out_3, not_4_out);
  _1_bit_memory _1_bit_memory_3 (.in_1(_1_bit_memory_2_out_3), .in_2(or_2_out), .out_3(_1_bit_memory_3_out_3));
  not not_4 (not_4_out, _1_bit_memory_4_out_3);
  _1_bit_memory _1_bit_memory_4 (.in_1(_1_bit_memory_3_out_3), .in_2(or_3_out), .out_3(_1_bit_memory_4_out_3));
  and and_2 (step_3, _1_bit_memory_4_out_3, not_5_out);
  _1_bit_memory _1_bit_memory_5 (.in_1(_1_bit_memory_4_out_3), .in_2(or_2_out), .out_3(_1_bit_memory_5_out_3));
  not not_5 (not_5_out, _1_bit_memory_6_out_3);
  _1_bit_memory _1_bit_memory_6 (.in_1(_1_bit_memory_5_out_3), .in_2(or_3_out), .out_3(_1_bit_memory_6_out_3));
  and and_3 (step_4, _1_bit_memory_6_out_3, not_6_out);
  not not_6 (not_6_out, _1_bit_memory_8_out_3);
  _1_bit_memory _1_bit_memory_7 (.in_1(_1_bit_memory_6_out_3), .in_2(or_2_out), .out_3(_1_bit_memory_7_out_3));
  _1_bit_memory _1_bit_memory_8 (.in_1(_1_bit_memory_7_out_3), .in_2(or_3_out), .out_3(_1_bit_memory_8_out_3));
  and and_4 (step_5, _1_bit_memory_8_out_3, not_7_out);
  not not_7 (not_7_out, _1_bit_memory_10_out_3);
  _1_bit_memory _1_bit_memory_9 (.in_1(_1_bit_memory_8_out_3), .in_2(or_2_out), .out_3(_1_bit_memory_9_out_3));
  _1_bit_memory _1_bit_memory_10 (.in_1(_1_bit_memory_9_out_3), .in_2(or_3_out), .out_3(_1_bit_memory_10_out_3));
  and and_5 (step_6, _1_bit_memory_10_out_3, not_8_out);
  _1_bit_memory _1_bit_memory_11 (.in_1(_1_bit_memory_10_out_3), .in_2(or_3_out), .out_3(_1_bit_memory_11_out_3));
  not not_8 (not_8_out, step_7);
  _1_bit_memory _1_bit_memory_12 (.in_1(_1_bit_memory_11_out_3), .in_2(or_2_out), .out_3(step_7));

  // Notes on the sheet:
  //   What is this Stepper useful for?
  //   The stepper is a 12-bit one-hot state machine (S1 to S12) that controls the timing of the CPU’s operations. It consists of 12 flip-flops arranged in a ring, where only one output is high (1) at a time, and the high signal shifts from S1 to S2, S2 to S3, ..., S12 to S1 with each clock cycle.
  //   Each step corresponds to a specific action in the fetch-execute cycle (e.g., S1–S3 for fetching, S4–S6 for execution, S7 for reset). The stepper ensures that the control unit performs each task in the correct order by activating the appropriate control signals at each step.
endmodule

module Fetch_Circuit (
  input  in_1,
  output BUS_1,
  output IR,
  output IAR_e,
  output MAR,
  output RAM,
  output IAR_s,
  output ACC_e,
  output ACC_s
);

  wire clock_we_gonna_use_1_clk, clock_we_gonna_use_1_clk_e, clock_we_gonna_use_1_clk_s, stepper_1_step_2,
       stepper_1_step_3;

  and and_1 (IR, clock_we_gonna_use_1_clk_s, stepper_1_step_2);
  and and_2 (MAR, clock_we_gonna_use_1_clk_s, BUS_1);
  and and_3 (IAR_s, clock_we_gonna_use_1_clk_s, stepper_1_step_3);
  and and_4 (ACC_s, clock_we_gonna_use_1_clk_s, BUS_1);
  _8_bit_register u_8_bit_register_1 (.s(IR));  // open: i0, i1, i2, i3, i4, i5, i6, i7, e, o0, o1, o2, o3, o4, o5, o6, o7
  Stepper stepper_1 (
    .reset(in_1), .in_2(clock_we_gonna_use_1_clk), .step_1(BUS_1), .step_2(stepper_1_step_2),
    .step_3(stepper_1_step_3));  // open: step_4, step_5, step_6, step_7
  clock_we_gonna_use clock_we_gonna_use_1 (
    .clk(clock_we_gonna_use_1_clk), .clk_e(clock_we_gonna_use_1_clk_e), .clk_s(clock_we_gonna_use_1_clk_s));
  and and_5 (IAR_e, clock_we_gonna_use_1_clk_e, BUS_1);
  and and_6 (RAM, clock_we_gonna_use_1_clk_e, stepper_1_step_2);
  and and_7 (ACC_e, clock_we_gonna_use_1_clk_e, stepper_1_step_3);

  // Notes on the sheet:
  //   Critical Note:
  //   All are Setters
  //   Step 1:
  //   Step 2:
  //   Step 3:
  //   https://github.com/hossamIII/But-How-Do-it-Know--logisim-version-.git
  //   Instruction Register (IR)
  //   The stepper’s first three steps are shown here, and result in ‘fetching’ the next ‘instruction’ from RAM.
  //   Here are the details of exactly how steps 1, 2 and 3 result in fetching an instruction in our little computer:
  //   This idea of putting a series of instructions in RAM and having the CPU execute them is a great invention.
  //   Thus, the contents of IAR will be placed on the bus during ‘clk e’ and set into MAR during ‘clk s.’
  //   Before diving into the Fetch Circuit, I strongly recommend reading the PDF titled "the brain of the computer.pdf" located in the project repository at
  //   This document provides a breakdown of the Control Unit(Computer's Brain), and will give you an intuitive understanding of what are the following circuits about.
  //   The bottom of this diagram includes the Instruction Register. Notice that we have given numbers to the individual bits of the IR, 0 at the left through 7 on the right. We will be referring to the individual bits soon.
  //   Then the rest of the steps ‘execute’ the ‘instruction.’ Exactly what will be done in steps 4, 5 and 6, is determined by the contents of the instruction that was fetched. Then the stepper starts over, fetches the next instruction, and executes it.
  //   We need to finish updating IAR. We added 1 to it in step 1, but the answer is still in ACC. It needs to be moved to IAR before the beginning of the next instruction cycle. So you can see the wire coming out of step 3 is connected to ‘enable’ of ACC and ‘set’ of IAR.
  //   Enables the currently selected byte in RAM onto the bus, and sets it into IR. This is the instruction that we will ‘execute’ in steps 4, 5 and 6 of this instruction cycle. In the diagram, you can see that the wire coming from step 2 is connected to the ‘enable’ of RAM and the ‘set’ of IR.
  //   The main thing we want to do is to get the address in IAR over to MAR. This is the address of the next instruction that we want to fetch from RAM. If you look at the wire coming out of step 1 of the stepper, you can see that two of the places it is connected to are the ‘enable’ of IAR and the ‘set’ of MAR.
  //   By the time we get to step 4, the instruction has already been moved from RAM to IR, and now steps 4, 5 and 6 can then do whatever is called for by the contents of IR. When that operation is done and the stepper is reset, the sequence will start over again, but now IAR has had 1 added to it, so the instruction at the next RAM address will be fetched and executed.
endmodule

module Instruction_Decode_Circuit (
);


  // Notes on the sheet:
  //   Now here’s a scary idea:
  //   And our computer might be able to ‘understand’ a code like this
  //   0000 0000 = Walk to the counter
  //   0000 0001 = Say “May I take your order?”
  //   0000 0010 = Listen to the answer
  //   0000 0100 = Press the fries button.
  //   0000 0101 = Press the milk button.
  //   Then you could express the sequence of an employee’s actions as a sequence of bytes.
  //   0100 0010 = If customer is not answering, go to step 2.
  //   0000 0011 = Press the cheeseburger button.
  //   0100 1001 = If customer does not say fries, go to step 9.
  //   0100 1011 = If customer does not say milk, go to step 11.
  //   and so on ..
  //   0100 0111 = If customer doesn’t say cheeseburger, go to step 7.
  //   Now we have a list of all of the possible actions that an employee might take, and a code that represents each one of them:
  //   First we make up a code table. We write some codes down the left side of the page. Then we decide what we want those codes to mean, and write those meanings next to the codes. 
  //   Now lets say that there are 256 or less individual actions involved in the job of working at such an establishment. You could then invent a code that would associate one of the states of a byte with each of the individual activities of an employee.
  //   Imagine that the job that an employee does at a fast food restaurant gets broken down into its individual elements. Walk to the counter, say “May I take your order?” listen to the answer, press the “cheeseburger” button on the cash register, etc.
  //   I hope nobody ever tries to make the employees of a fast food restaurant learn a code like this. People don’t take well to being so mechanized. But maybe someone will try to staff one of these restaurants with robots someday. In that case, the robots would probably work better using this sort of a code.
endmodule

module ALU_Execute_Circuit (
  input  clk_e,
  input  Reg_B,
  input  clk_s,
  input  Reg_B_2,
  input  Reg_A,
  input  in_6,
  input  in_7,
  input  in_8,
  input  in_9,
  input  in_10,
  input  in_11,
  input  in_12,
  input  in_13,
  input  in_14,
  input  in_15,
  output R0,
  output R0_2,
  output R1,
  output R1_2,
  output R2,
  output R2_2,
  output R3,
  output R3_2
);

  wire and_1_out, and_2_out, and_3_out, and_4_out, and_5_out, and_6_out, and_7_out, and_8_out,
       decoder_1_out0, decoder_1_out1, decoder_1_out2, decoder_1_out3, decoder_2_out0, decoder_2_out1,
       decoder_2_out2, decoder_2_out3, decoder_3_out0, decoder_3_out1, decoder_3_out2, decoder_3_out3;
  wire [1:0] n8_bit_register_1_o4, n8_bit_register_1_o6, undriven;

  or or_1 (R0_2, and_1_out, and_5_out);
  or or_2 (R1_2, and_2_out, and_6_out);
  or or_3 (R2_2, and_3_out, and_7_out);
  or or_4 (R3_2, and_4_out, and_8_out);
  and and_1 (and_1_out, clk_e, Reg_B_2, decoder_1_out0);
  and and_2 (and_2_out, clk_e, Reg_B_2, decoder_1_out1);
  and and_3 (and_3_out, clk_e, Reg_B_2, decoder_1_out2);
  and and_4 (and_4_out, clk_e, Reg_B_2, decoder_1_out3);
  and and_5 (and_5_out, clk_e, Reg_A, decoder_2_out0);
  and and_6 (and_6_out, clk_e, Reg_A, decoder_2_out1);
  and and_7 (and_7_out, clk_e, Reg_A, decoder_2_out2);
  and and_8 (and_8_out, clk_e, Reg_A, decoder_2_out3);
  Decoder #(.select(2)) decoder_1 (
    .out0(decoder_1_out0), .out1(decoder_1_out1), .out2(decoder_1_out2), .out3(decoder_1_out3), .sel(undriven));  // open: en
  Decoder #(.select(2)) decoder_2 (
    .out0(decoder_2_out0), .out1(decoder_2_out1), .out2(decoder_2_out2), .out3(decoder_2_out3),
    .sel(n8_bit_register_1_o4));  // open: en
  _8_bit_register u_8_bit_register_1 (
    .i0(in_8), .i1(in_9), .i2(in_10), .i3(in_11), .i4(in_12), .i5(in_13), .i6(in_14), .i7(in_15), .e(in_7),
    .s(in_6), .o4(n8_bit_register_1_o4[0]), .o5(n8_bit_register_1_o4[1]), .o6(n8_bit_register_1_o6[0]),
    .o7(n8_bit_register_1_o6[1]));  // open: o0, o1, o2, o3
  Decoder #(.select(2)) decoder_3 (
    .out0(decoder_3_out0), .out1(decoder_3_out1), .out2(decoder_3_out2), .out3(decoder_3_out3), .sel(undriven));  // open: en
  and and_9 (R0, clk_s, Reg_B, decoder_3_out0);
  and and_10 (R1, clk_s, Reg_B, decoder_3_out1);
  and and_11 (R2, clk_s, Reg_B, decoder_3_out2);
  and and_12 (R3, clk_s, Reg_B, decoder_3_out3);

  // Notes on the sheet:
  //   Step 4:
  //   Step 5:
  //   Step 6:
  //   storing the result in the Accumulator (ACC).
  //   one from Register A (Reg A, selected by IR bits 4–5) and one from Register B (Reg B, selected by IR bits 6–7).
  //   Here are the details of exactly how steps 4, 5 and 6 perfom the operation determined by IR bits 1-3:
  //   This is where the magic of math happens!
  //   This phase uses the Arithmetic Logic Unit (ALU) to perform operations like ADD, SUB, AND, OR, NOT, or CMP on two operands:
  //   Reg B’s value is enabled onto the bus and set into the Temporary Register (TMP).
  //   Reg A’s value is enabled onto the bus, and the ALU performs the operation (with Reg A and TMP as inputs),
  //   the result in ACC is enabled onto the bus and set back into Reg B (unless the operation is CMP, which skips this step).
  //   The ALU Execution phase occurs during steps 4–6 of the fetch-execute cycle when the instruction in the Instruction Register (IR) indicates an ALU operation (IR bit 0 = 1).
endmodule

module Load_Store_Execute_Circuit (
  input  in_1,
  input  in_2,
  input  in_3,
  input  in_4,
  input  in_5,
  input  in_6,
  input  in_7,
  input  in_8,
  input  in_9,
  input  in_10,
  input  in_11,
  output REG_A,
  output MAR,
  output RAM,
  output REG_B,
  output REG_A_2,
  output MAR_2,
  output REG_B_2,
  output RAM_2,
  output o4,
  output o5,
  output o6,
  output o7
);

  wire and_1_out, and_2_out, clock_1_out, decoder_1_out0, decoder_1_out1, decoder_1_out2, decoder_1_out3,
       decoder_1_out4, decoder_1_out5, decoder_1_out6, decoder_1_out7, n8_bit_register_1_o0, not_1_out,
       stepper_1_step_4, stepper_1_step_5;
  wire [2:0] n8_bit_register_1_o3;

  not not_1 (not_1_out, n8_bit_register_1_o0);
  Decoder #(.select(3)) decoder_1 (
    .out0(decoder_1_out0), .out1(decoder_1_out1), .out2(decoder_1_out2), .out3(decoder_1_out3),
    .out4(decoder_1_out4), .out5(decoder_1_out5), .out6(decoder_1_out6), .out7(decoder_1_out7),
    .sel(n8_bit_register_1_o3));  // open: en
  _8_bit_register u_8_bit_register_1 (
    .i0(in_4), .i1(in_5), .i2(in_6), .i3(in_7), .i4(in_8), .i5(in_9), .i6(in_10), .i7(in_11), .e(in_3),
    .s(in_2), .o0(n8_bit_register_1_o0), .o1(n8_bit_register_1_o3[2]), .o2(n8_bit_register_1_o3[1]),
    .o3(n8_bit_register_1_o3[0]), .o4(o4), .o5(o5), .o6(o6), .o7(o7));
  and and_1 (and_1_out, not_1_out, decoder_1_out0);
  and and_2 (and_2_out, not_1_out, decoder_1_out1);
  // AND_Gate and_3 has open pins: in0=not_1_out, in1=decoder_1_out2, out=open
  // AND_Gate and_4 has open pins: in0=not_1_out, in1=decoder_1_out3, out=open
  // AND_Gate and_5 has open pins: in0=not_1_out, in1=decoder_1_out4, out=open
  // AND_Gate and_6 has open pins: in0=not_1_out, in1=decoder_1_out5, out=open
  // AND_Gate and_7 has open pins: in0=not_1_out, in1=decoder_1_out6, out=open
  // AND_Gate and_8 has open pins: in0=not_1_out, in1=decoder_1_out7, out=open
  Stepper stepper_1 (
    .reset(in_1), .in_2(clock_1_out), .step_4(stepper_1_step_4), .step_5(stepper_1_step_5));  // open: step_1, step_2, step_3, step_6, step_7
  and and_9 (MAR, stepper_1_step_4, and_1_out);
  and and_10 (MAR_2, stepper_1_step_4, and_2_out);
  Clock clock_1 (.out(clock_1_out));
  and and_11 (RAM, stepper_1_step_5, and_2_out);
  and and_12 (RAM_2, stepper_1_step_5, and_2_out);

  assign REG_A = MAR;
  assign REG_A_2 = MAR_2;
  assign REG_B = RAM;
  assign REG_B_2 = RAM_2;

  // Notes on the sheet:
  //   Enables
  //   The Load and Store instructions move a byte between RAM and a register, and they’re very similar, so we’ll cover them together.
  //   AND gates on the decoder outputs, controlled by the NOT gate, ensure only non-ALU instructions activate the right gates to move data between RAM and registers.
  //   Sets
  //   To identify a Load or Store instruction in the Instruction Register (IR), we use a NOT gate on bit 0: if bit 0 is off, it’s a non-ALU instruction. IR bits 1–3 go to a 3x8 decoder, which selects the instruction type (e.g., Load or Store).
endmodule

module Data_Execute_Circuit (
  input  in_1,
  input  in_2,
  input  in_3,
  input  in_4,
  input  in_5,
  input  in_6,
  input  in_7,
  input  in_8,
  input  in_9,
  input  in_10,
  input  in_11,
  output BUS_1,
  output MAR,
  output IAR_e,
  output ACC_s,
  output RAM_e,
  output REG_B,
  output ACC_e,
  output IAR,
  output o4,
  output o5,
  output o6,
  output o7
);

  wire and_3_out, clock_1_out, decoder_1_out0, decoder_1_out1, decoder_1_out2, decoder_1_out3,
       decoder_1_out4, decoder_1_out5, decoder_1_out6, decoder_1_out7, n8_bit_register_1_o0, not_1_out,
       stepper_1_step_5, stepper_1_step_6;
  wire [2:0] n8_bit_register_1_o3;

  not not_1 (not_1_out, n8_bit_register_1_o0);
  Decoder #(.select(3)) decoder_1 (
    .out0(decoder_1_out0), .out1(decoder_1_out1), .out2(decoder_1_out2), .out3(decoder_1_out3),
    .out4(decoder_1_out4), .out5(decoder_1_out5), .out6(decoder_1_out6), .out7(decoder_1_out7),
    .sel(n8_bit_register_1_o3));  // open: en
  _8_bit_register u_8_bit_register_1 (
    .i0(in_4), .i1(in_5), .i2(in_6), .i3(in_7), .i4(in_8), .i5(in_9), .i6(in_10), .i7(in_11), .e(in_3),
    .s(in_2), .o0(n8_bit_register_1_o0), .o1(n8_bit_register_1_o3[2]), .o2(n8_bit_register_1_o3[1]),
    .o3(n8_bit_register_1_o3[0]), .o4(o4), .o5(o5), .o6(o6), .o7(o7));
  // AND_Gate and_1 has open pins: in0=not_1_out, in1=decoder_1_out0, out=open
  // AND_Gate and_2 has open pins: in0=not_1_out, in1=decoder_1_out1, out=open
  and and_3 (and_3_out, not_1_out, decoder_1_out2);
  // AND_Gate and_4 has open pins: in0=not_1_out, in1=decoder_1_out3, out=open
  // AND_Gate and_5 has open pins: in0=not_1_out, in1=decoder_1_out4, out=open
  // AND_Gate and_6 has open pins: in0=not_1_out, in1=decoder_1_out5, out=open
  // AND_Gate and_7 has open pins: in0=not_1_out, in1=decoder_1_out6, out=open
  // AND_Gate and_8 has open pins: in0=not_1_out, in1=decoder_1_out7, out=open
  Stepper stepper_1 (
    .reset(in_1), .in_2(clock_1_out), .step_5(stepper_1_step_5), .step_6(stepper_1_step_6));  // open: step_1, step_2, step_3, step_4, step_7
  and and_9 (ACC_e, stepper_1_step_6, and_3_out);
  Clock clock_1 (.out(clock_1_out));
  and and_10 (RAM_e, stepper_1_step_5, and_3_out);
  and and_11 (ACC_s, ACC_s, and_3_out);

  assign BUS_1 = ACC_s;
  assign IAR = ACC_e;
  assign IAR_e = ACC_s;
  assign MAR = ACC_s;
  assign REG_B = RAM_e;

  // Notes on the sheet:
  //   Enables
  //   In step 6, ACC updates IAR to skip the data byte and point to the next instruction.
  //   Since IAR already points to this data after fetching, in step 4, we send IAR to MAR, enable Bus 1 to add 1 to IAR via the ALU, and set the result in ACC. In step 5, RAM’s data goes to the register.
  //   Sets
  //   The Data instruction loads a byte from RAM into a register, but the byte comes from the next instruction’s spot, making this a two-byte instruction: the first byte is the instruction (bits 0–3 as 0010, bits 6–7 select the register), and the second byte is the data.
endmodule

module Flags (
  input  in_1,
  input  carry_out,
  input  a_larger,
  input  equal,
  input  zero,
  input  in_6,
  input  in_7,
  input  in_8,
  input  in_9,
  input  in_10,
  input  in_11,
  input  in_12,
  input  in_13,
  input  in_14,
  input  in_15,
  output BUS_1,
  output MAR,
  output IAR_e,
  output ACC_s,
  output RAM_e,
  output REG_B,
  output ACC_e,
  output IAR
);

  wire and_3_out, and_10_out, and_11_out, and_12_out, and_13_out, clock_1_out, decoder_1_out0,
       decoder_1_out1, decoder_1_out2, decoder_1_out3, decoder_1_out4, decoder_1_out5, decoder_1_out6,
       decoder_1_out7, n8_bit_register_1_o0, n8_bit_register_1_o4, n8_bit_register_1_o5,
       n8_bit_register_1_o6, n8_bit_register_1_o7, not_1_out, or_1_out, stepper_1_step_5, stepper_1_step_6;
  wire [2:0] n8_bit_register_1_o3;

  not not_1 (not_1_out, n8_bit_register_1_o0);
  Decoder #(.select(3)) decoder_1 (
    .out0(decoder_1_out0), .out1(decoder_1_out1), .out2(decoder_1_out2), .out3(decoder_1_out3),
    .out4(decoder_1_out4), .out5(decoder_1_out5), .out6(decoder_1_out6), .out7(decoder_1_out7),
    .sel(n8_bit_register_1_o3));  // open: en
  _8_bit_register u_8_bit_register_1 (
    .i0(in_8), .i1(in_9), .i2(in_10), .i3(in_11), .i4(in_12), .i5(in_13), .i6(in_14), .i7(in_15), .e(in_7),
    .s(in_6), .o0(n8_bit_register_1_o0), .o1(n8_bit_register_1_o3[2]), .o2(n8_bit_register_1_o3[1]),
    .o3(n8_bit_register_1_o3[0]), .o4(n8_bit_register_1_o4), .o5(n8_bit_register_1_o5),
    .o6(n8_bit_register_1_o6), .o7(n8_bit_register_1_o7));
  // AND_Gate and_1 has open pins: in0=not_1_out, in1=decoder_1_out0, out=open
  // AND_Gate and_2 has open pins: in0=not_1_out, in1=decoder_1_out1, out=open
  and and_3 (and_3_out, not_1_out, decoder_1_out2);
  // AND_Gate and_4 has open pins: in0=not_1_out, in1=decoder_1_out3, out=open
  // AND_Gate and_5 has open pins: in0=not_1_out, in1=decoder_1_out4, out=open
  // AND_Gate and_6 has open pins: in0=not_1_out, in1=decoder_1_out5, out=open
  // AND_Gate and_7 has open pins: in0=not_1_out, in1=decoder_1_out6, out=open
  // AND_Gate and_8 has open pins: in0=not_1_out, in1=decoder_1_out7, out=open
  Stepper stepper_1 (
    .reset(in_1), .in_2(clock_1_out), .step_5(stepper_1_step_5), .step_6(stepper_1_step_6));  // open: step_1, step_2, step_3, step_4, step_7
  and and_9 (ACC_e, stepper_1_step_6, or_1_out, and_3_out);
  and and_10 (and_10_out, n8_bit_register_1_o4, carry_out);
  and and_11 (and_11_out, n8_bit_register_1_o5, a_larger);
  and and_12 (and_12_out, n8_bit_register_1_o6, equal);
  and and_13 (and_13_out, n8_bit_register_1_o7, zero);
  Clock clock_1 (.out(clock_1_out));
  and and_14 (RAM_e, stepper_1_step_5, and_3_out);
  and and_15 (ACC_s, ACC_s, and_3_out);
  or or_1 (or_1_out, and_10_out, and_11_out, and_12_out, and_13_out);

  assign BUS_1 = ACC_s;
  assign IAR = ACC_e;
  assign IAR_e = ACC_s;
  assign MAR = ACC_s;
  assign REG_B = RAM_e;

  // Notes on the sheet:
  //   Enables
  //   if any tested flag is on, the CPU jumps to the address in the second byte.
  //   This flag-jump mechanism is a key invention for how computers work.
  //   Sets
  //   The Flag Register is the last register added to the CPU, using four bits to store the ALU’s flags (carry, larger, equal, zero) like a vehicule dashboard warning lights that will warn you if there is something wrong with the battery, airbag, engine oil...
  //   It’s set during step 5 of an ALU instruction, alongside the ACC, and holds its value until the next ALU instruction. This allows “Jump If” instructions to use the flags to decide whether to jump, based on the second four bits of the instruction, which specify which flags to check.
endmodule

module Ta_daa (
);


  // Notes on the sheet:
  //   Critical Note:
  //   https://github.com/hossamIII/But-How-Do-it-Know--logisim-version-.git
  //   This PDF introduces I/O operations, peripherals, and the philosophical limits of digital computers, providing context for enhancing the control unit’s functionality.
  //   For a deeper understanding of how the control unit can be extended to communicate with the outside world (e.g., via keyboards or displays), refer to "how can we use this computer to communicate with the outside world.pdf" in the project repository at
endmodule

module _8_bit_register (
  input  i0,
  input  i1,
  input  i2,
  input  i3,
  input  i4,
  input  i5,
  input  i6,
  input  i7,
  input  e,
  input  s,
  output o0,
  output o1,
  output o2,
  output o3,
  output o4,
  output o5,
  output o6,
  output o7
);

  wire and_1_out, and_2_out, and_3_out, and_4_out, and_5_out, and_6_out, and_7_out, and_8_out;

  and and_1 (and_1_out, i0, e);
  and and_2 (and_2_out, i1, e);
  and and_3 (and_3_out, i2, e);
  and and_4 (and_4_out, i3, e);
  and and_5 (and_5_out, i4, e);
  and and_6 (and_6_out, i5, e);
  and and_7 (and_7_out, i6, e);
  and and_8 (and_8_out, i7, e);
  Ta_daa ta_daa_1 ();

  // Notes on the sheet:
  //   Enabler
  //   |
  //   |
  //   |
  //   |
  //   |
  //   |
  //   |
  //   |
  //   |
  //   |
  //   |
  //   |
  //   A byte of memory
endmodule

module Enabler (
  input  i0,
  input  i1,
  input  i2,
  input  i3,
  input  i4,
  input  i5,
  input  i6,
  input  i7,
  input  s,
  output o0,
  output o1,
  output o2,
  output o3,
  output o4,
  output o5,
  output o6,
  output o7
);

  _1_bit_memory u_1_bit_memory_1 (.in_1(i0), .in_2(s), .out_3(o0));
  _1_bit_memory u_1_bit_memory_2 (.in_1(i1), .in_2(s), .out_3(o1));
  _1_bit_memory u_1_bit_memory_3 (.in_1(i2), .in_2(s), .out_3(o2));
  _1_bit_memory u_1_bit_memory_4 (.in_1(i3), .in_2(s), .out_3(o3));
  _1_bit_memory u_1_bit_memory_5 (.in_1(i4), .in_2(s), .out_3(o4));
  _1_bit_memory u_1_bit_memory_6 (.in_1(i5), .in_2(s), .out_3(o5));
  _1_bit_memory u_1_bit_memory_7 (.in_1(i6), .in_2(s), .out_3(o6));
  _1_bit_memory u_1_bit_memory_8 (.in_1(i7), .in_2(s), .out_3(o7));

  // Notes on the sheet:
  //   A bit of memory
  //   A bit of memory
  //   A bit of memory
  //   A bit of memory
  //   A bit of memory
  //   A bit of memory
  //   A bit of memory
  //   A bit of memory
endmodule
